// Logisim project LED_Display.circ as structural Verilog: 2 circuits, main circuit main
module main (
  input  [7:0] DATA,
  input  [7:0] ADDRESS,
  input  in_3
);

  wire clock_1_out, clock_2_out, comparator_1_gt, COMPARE, decoder_1_out0, decoder_1_out1, decoder_1_out2,
       decoder_1_out3, decoder_2_out0, decoder_2_out1, decoder_2_out2, decoder_2_out3, decoder_3_out0,
       decoder_3_out1, decoder_3_out2, decoder_3_out3, decoder_3_out4, decoder_3_out5, decoder_3_out6,
       decoder_3_out7, decoder_4_out0, decoder_4_out1, decoder_4_out2, decoder_4_out3, decoder_4_out4,
       decoder_4_out5, decoder_4_out6, decoder_4_out7, decoder_5_out0, decoder_5_out1, decoder_5_out2,
       decoder_5_out3, decoder_5_out4, decoder_5_out5, decoder_5_out6, decoder_5_out7, decoder_6_out0,
       decoder_6_out1, decoder_6_out2, decoder_6_out3, decoder_6_out4, decoder_6_out5, decoder_6_out6,
       decoder_6_out7, not_2_out, not_3_out, not_5_out, not_6_out, not_7_out, not_8_out, not_9_out,
       not_10_out, not_11_out, not_12_out, not_13_out, not_14_out, not_15_out, not_16_out, not_17_out,
       not_18_out, not_19_out, not_20_out, not_21_out, not_22_out, not_23_out, not_24_out, not_25_out,
       not_26_out, not_27_out, not_28_out, not_29_out, not_30_out, not_31_out, not_32_out, not_33_out,
       not_34_out, not_35_out, not_36_out, not_37_out, not_38_out, not_39_out, not_40_out, not_41_out,
       not_42_out, not_43_out, not_44_out, or_2_out, pull_resistor_1_node, pull_resistor_3_node,
       pull_resistor_4_node, pull_resistor_5_node, READ_B, six_1_q0, six_1_q1, six_1_q2, six_1_q4, six_1_q5,
       six_1_q6, six_2_q0, six_2_q1, six_2_q2, six_2_q4, six_2_q5, six_2_q6, six_3_q0, six_3_q1, six_3_q2,
       six_3_q4, six_3_q5, six_3_q6, six_4_q0, six_4_q1, six_4_q2, six_4_q4, six_4_q5, six_4_q6, six_5_q0,
       six_5_q1, six_5_q2, six_5_q4, six_5_q5, six_5_q6, six_6_q0, six_6_q1, six_6_q2, six_6_q4, six_6_q5,
       six_6_q6, six_7_q0, six_7_q1, six_7_q2, six_7_q4, six_7_q5, six_7_q6, six_8_q0, six_8_q1, six_8_q2,
       six_8_q4, six_8_q5, six_8_q6, six_9_q0, six_9_q1, six_9_q2, six_9_q4, six_9_q5, six_9_q6, six_10_q0,
       six_10_q1, six_10_q2, six_10_q4, six_10_q5, six_10_q6, six_11_q0, six_11_q1, six_11_q2, six_11_q4,
       six_11_q5, six_11_q6, six_12_q0, six_12_q1, six_12_q2, six_12_q4, six_12_q5, six_12_q6, six_13_q0,
       six_13_q1, six_13_q2, six_13_q4, six_13_q5, six_13_q6, six_14_q0, six_14_q1, six_14_q2, six_14_q4,
       six_14_q5, six_14_q6, six_15_q0, six_15_q1, six_15_q2, six_15_q4, six_15_q5, six_15_q6, six_16_q0,
       six_16_q1, six_16_q2, six_16_q4, six_16_q5, six_16_q6, six_17_q0, six_17_q1, six_17_q2, six_17_q4,
       six_17_q5, six_17_q6, six_18_q0, six_18_q1, six_18_q2, six_18_q4, six_18_q5, six_18_q6, six_19_q0,
       six_19_q1, six_19_q2, six_19_q4, six_19_q5, six_19_q6, six_20_q0, six_20_q1, six_20_q2, six_20_q4,
       six_20_q5, six_20_q6, six_21_q0, six_21_q1, six_21_q2, six_21_q4, six_21_q5, six_21_q6, six_22_q0,
       six_22_q1, six_22_q2, six_22_q4, six_22_q5, six_22_q6, six_23_q0, six_23_q1, six_23_q2, six_23_q4,
       six_23_q5, six_23_q6, six_24_q0, six_24_q1, six_24_q2, six_24_q4, six_24_q5, six_24_q6, six_25_q0,
       six_25_q1, six_25_q2, six_25_q4, six_25_q5, six_25_q6, six_26_q0, six_26_q1, six_26_q2, six_26_q4,
       six_26_q5, six_26_q6, six_27_q0, six_27_q1, six_27_q2, six_27_q4, six_27_q5, six_27_q6, six_28_q0,
       six_28_q1, six_28_q2, six_28_q4, six_28_q5, six_28_q6, six_29_q0, six_29_q1, six_29_q2, six_29_q4,
       six_29_q5, six_29_q6, six_30_q0, six_30_q1, six_30_q2, six_30_q4, six_30_q5, six_30_q6, six_31_q0,
       six_31_q1, six_31_q2, six_31_q4, six_31_q5, six_31_q6, six_32_q0, six_32_q1, six_32_q2, six_32_q4,
       six_32_q5, six_32_q6, WRITE_B;
  wire [1:0] pull_resistor_7_node, STAGE;
  wire [5:0] STROBE;
  wire [6:0] pull_resistor_2_node, pull_resistor_6_node;
  wire [7:0] PIXEL, RGB_24_Bit_Colour_data;
  wire [15:0] register_1_q;

  Clock clock_1 (.out(clock_1_out));
  Counter #(.max('hffff), .width(16)) counter_1 (
    .Q({STROBE, PIXEL, STAGE}), .clk(clock_1_out));  // open: load, D, count, carry, up, clr
  not not_1 (READ_B, decoder_1_out0);
  not not_2 (not_2_out, decoder_1_out1);
  not not_3 (not_3_out, decoder_1_out2);
  not not_4 (WRITE_B, decoder_1_out3);
  Decoder #(.select(2)) decoder_1 (
    .out0(decoder_1_out0), .out1(decoder_1_out1), .out2(decoder_1_out2), .out3(decoder_1_out3), .sel(STAGE));  // open: en
  Register #(.width(16)) register_1 (.D({ADDRESS, DATA}), .Q(register_1_q), .clk(in_3));  // open: en, clr
  D_Flip_Flop d_ff_1 (.clk(in_3), .D(pull_resistor_1_node));  // open: Q, Qn, preset, reset
  Pull_Resistor #(.pull(1)) pull_resistor_1 (.node(pull_resistor_1_node));
  or or_1 (COMPARE, not_2_out, not_3_out);
  Pull_Resistor pull_resistor_2 (.node(pull_resistor_2_node));
  RAM #(.addrWidth(15), .databus("bidir"), .enables("line"), .trigger("high")) ram_1 (
    .addr({pull_resistor_2_node, register_1_q[15:8]}), .data(register_1_q[7:0]));  // open: we, oe, clk
  Pull_Resistor pull_resistor_3 (.node(pull_resistor_3_node));
  Pull_Resistor pull_resistor_4 (.node(pull_resistor_4_node));
  Pull_Resistor #(.pull(1)) pull_resistor_5 (.node(pull_resistor_5_node));
  Pull_Resistor pull_resistor_6 (.node(pull_resistor_6_node));
  Pull_Resistor pull_resistor_7 (.node(pull_resistor_7_node));
  // Probe on register_1_q[7:0]
  ROM #(.addrWidth(15)) RGB_24_Bit_Colour (.addr({pull_resistor_6_node, PIXEL}), .data(RGB_24_Bit_Colour_data));
  // Probe on {STROBE, pull_resistor_7_node}
  Clock clock_2 (.out(clock_2_out));
  or or_2 (or_2_out, WRITE_B, clock_2_out);
  not not_5 (not_5_out, decoder_2_out0);
  not not_6 (not_6_out, decoder_2_out1);
  not not_7 (not_7_out, decoder_2_out2);
  not not_8 (not_8_out, decoder_2_out3);
  Decoder #(.select(2)) decoder_2 (
    .out0(decoder_2_out0), .out1(decoder_2_out1), .out2(decoder_2_out2), .out3(decoder_2_out3),
    .sel(PIXEL[7:6]));  // open: en
  // Probe on RGB_24_Bit_Colour_data
  Comparator #(.mode("unsigned")) comparator_1 (
    .a(RGB_24_Bit_Colour_data), .b({STROBE, pull_resistor_7_node}), .gt(comparator_1_gt));  // open: eq, lt
  Decoder #(.select(3)) decoder_3 (
    .out0(decoder_3_out0), .out1(decoder_3_out1), .out2(decoder_3_out2), .out3(decoder_3_out3),
    .out4(decoder_3_out4), .out5(decoder_3_out5), .out6(decoder_3_out6), .out7(decoder_3_out7),
    .sel(PIXEL[5:3]), .en(not_9_out));
  not not_9 (not_9_out, not_5_out);
  Decoder #(.select(3)) decoder_4 (
    .out0(decoder_4_out0), .out1(decoder_4_out1), .out2(decoder_4_out2), .out3(decoder_4_out3),
    .out4(decoder_4_out4), .out5(decoder_4_out5), .out6(decoder_4_out6), .out7(decoder_4_out7),
    .sel(PIXEL[5:3]), .en(not_10_out));
  not not_10 (not_10_out, not_6_out);
  Decoder #(.select(3)) decoder_5 (
    .out0(decoder_5_out0), .out1(decoder_5_out1), .out2(decoder_5_out2), .out3(decoder_5_out3),
    .out4(decoder_5_out4), .out5(decoder_5_out5), .out6(decoder_5_out6), .out7(decoder_5_out7),
    .sel(PIXEL[5:3]), .en(not_11_out));
  not not_11 (not_11_out, not_7_out);
  Decoder #(.select(3)) decoder_6 (
    .out0(decoder_6_out0), .out1(decoder_6_out1), .out2(decoder_6_out2), .out3(decoder_6_out3),
    .out4(decoder_6_out4), .out5(decoder_6_out5), .out6(decoder_6_out6), .out7(decoder_6_out7),
    .sel(PIXEL[5:3]), .en(not_12_out));
  not not_12 (not_12_out, not_8_out);
  not not_13 (not_13_out, decoder_3_out0);
  not not_14 (not_14_out, decoder_3_out1);
  not not_15 (not_15_out, decoder_3_out2);
  not not_16 (not_16_out, decoder_3_out3);
  not not_17 (not_17_out, decoder_3_out4);
  not not_18 (not_18_out, decoder_3_out5);
  not not_19 (not_19_out, decoder_3_out6);
  not not_20 (not_20_out, decoder_3_out7);
  not not_21 (not_21_out, decoder_4_out0);
  not not_22 (not_22_out, decoder_4_out1);
  not not_23 (not_23_out, decoder_4_out2);
  not not_24 (not_24_out, decoder_4_out3);
  not not_25 (not_25_out, decoder_4_out4);
  not not_26 (not_26_out, decoder_4_out5);
  not not_27 (not_27_out, decoder_4_out6);
  not not_28 (not_28_out, decoder_4_out7);
  not not_29 (not_29_out, decoder_5_out0);
  not not_30 (not_30_out, decoder_5_out1);
  not not_31 (not_31_out, decoder_5_out2);
  not not_32 (not_32_out, decoder_5_out3);
  not not_33 (not_33_out, decoder_5_out4);
  not not_34 (not_34_out, decoder_5_out5);
  not not_35 (not_35_out, decoder_5_out6);
  not not_36 (not_36_out, decoder_5_out7);
  not not_37 (not_37_out, decoder_6_out0);
  not not_38 (not_38_out, decoder_6_out1);
  not not_39 (not_39_out, decoder_6_out2);
  not not_40 (not_40_out, decoder_6_out3);
  not not_41 (not_41_out, decoder_6_out4);
  not not_42 (not_42_out, decoder_6_out5);
  not not_43 (not_43_out, decoder_6_out6);
  not not_44 (not_44_out, decoder_6_out7);
  six six_1 (
    .DATA(comparator_1_gt), .LE1_B(not_13_out), .LE2_B(or_2_out), .ADDRESS(PIXEL[2:0]), .Q0(six_1_q0),
    .Q1(six_1_q1), .Q2(six_1_q2), .Q4(six_1_q4), .Q5(six_1_q5), .Q6(six_1_q6));
  // RGBLED rgbled_1: pin names not known; wires that end beside it: six_1_q1, six_1_q0, six_1_q2
  six six_2 (
    .DATA(comparator_1_gt), .LE1_B(not_17_out), .LE2_B(or_2_out), .ADDRESS(PIXEL[2:0]), .Q0(six_2_q0),
    .Q1(six_2_q1), .Q2(six_2_q2), .Q4(six_2_q4), .Q5(six_2_q5), .Q6(six_2_q6));
  // RGBLED rgbled_2: pin names not known; wires that end beside it: six_2_q1, six_2_q0, six_2_q2
  six six_3 (
    .DATA(comparator_1_gt), .LE1_B(not_21_out), .LE2_B(or_2_out), .ADDRESS(PIXEL[2:0]), .Q0(six_3_q0),
    .Q1(six_3_q1), .Q2(six_3_q2), .Q4(six_3_q4), .Q5(six_3_q5), .Q6(six_3_q6));
  // RGBLED rgbled_3: pin names not known; wires that end beside it: six_3_q1, six_3_q0, six_3_q2
  six six_4 (
    .DATA(comparator_1_gt), .LE1_B(not_25_out), .LE2_B(or_2_out), .ADDRESS(PIXEL[2:0]), .Q0(six_4_q0),
    .Q1(six_4_q1), .Q2(six_4_q2), .Q4(six_4_q4), .Q5(six_4_q5), .Q6(six_4_q6));
  // RGBLED rgbled_4: pin names not known; wires that end beside it: six_4_q1, six_4_q0, six_4_q2
  six six_5 (
    .DATA(comparator_1_gt), .LE1_B(not_29_out), .LE2_B(or_2_out), .ADDRESS(PIXEL[2:0]), .Q0(six_5_q0),
    .Q1(six_5_q1), .Q2(six_5_q2), .Q4(six_5_q4), .Q5(six_5_q5), .Q6(six_5_q6));
  // RGBLED rgbled_5: pin names not known; wires that end beside it: six_5_q1, six_5_q0, six_5_q2
  six six_6 (
    .DATA(comparator_1_gt), .LE1_B(not_33_out), .LE2_B(or_2_out), .ADDRESS(PIXEL[2:0]), .Q0(six_6_q0),
    .Q1(six_6_q1), .Q2(six_6_q2), .Q4(six_6_q4), .Q5(six_6_q5), .Q6(six_6_q6));
  // RGBLED rgbled_6: pin names not known; wires that end beside it: six_6_q1, six_6_q0, six_6_q2
  six six_7 (
    .DATA(comparator_1_gt), .LE1_B(not_37_out), .LE2_B(or_2_out), .ADDRESS(PIXEL[2:0]), .Q0(six_7_q0),
    .Q1(six_7_q1), .Q2(six_7_q2), .Q4(six_7_q4), .Q5(six_7_q5), .Q6(six_7_q6));
  // RGBLED rgbled_7: pin names not known; wires that end beside it: six_7_q1, six_7_q0, six_7_q2
  six six_8 (
    .DATA(comparator_1_gt), .LE1_B(not_41_out), .LE2_B(or_2_out), .ADDRESS(PIXEL[2:0]), .Q0(six_8_q0),
    .Q1(six_8_q1), .Q2(six_8_q2), .Q4(six_8_q4), .Q5(six_8_q5), .Q6(six_8_q6));
  // RGBLED rgbled_8: pin names not known; wires that end beside it: six_8_q1, six_8_q0, six_8_q2
  // RGBLED rgbled_9: pin names not known; wires that end beside it: six_1_q5, six_1_q4, six_1_q6
  // RGBLED rgbled_10: pin names not known; wires that end beside it: six_2_q5, six_2_q4, six_2_q6
  // RGBLED rgbled_11: pin names not known; wires that end beside it: six_3_q5, six_3_q4, six_3_q6
  // RGBLED rgbled_12: pin names not known; wires that end beside it: six_4_q5, six_4_q4, six_4_q6
  // RGBLED rgbled_13: pin names not known; wires that end beside it: six_5_q5, six_5_q4, six_5_q6
  // RGBLED rgbled_14: pin names not known; wires that end beside it: six_6_q5, six_6_q4, six_6_q6
  // RGBLED rgbled_15: pin names not known; wires that end beside it: six_7_q5, six_7_q4, six_7_q6
  // RGBLED rgbled_16: pin names not known; wires that end beside it: six_8_q5, six_8_q4, six_8_q6
  six six_9 (
    .DATA(comparator_1_gt), .LE1_B(not_14_out), .LE2_B(or_2_out), .ADDRESS(PIXEL[2:0]), .Q0(six_9_q0),
    .Q1(six_9_q1), .Q2(six_9_q2), .Q4(six_9_q4), .Q5(six_9_q5), .Q6(six_9_q6));
  // RGBLED rgbled_17: pin names not known; wires that end beside it: six_9_q1, six_9_q0, six_9_q2
  six six_10 (
    .DATA(comparator_1_gt), .LE1_B(not_18_out), .LE2_B(or_2_out), .ADDRESS(PIXEL[2:0]), .Q0(six_10_q0),
    .Q1(six_10_q1), .Q2(six_10_q2), .Q4(six_10_q4), .Q5(six_10_q5), .Q6(six_10_q6));
  // RGBLED rgbled_18: pin names not known; wires that end beside it: six_10_q1, six_10_q0, six_10_q2
  six six_11 (
    .DATA(comparator_1_gt), .LE1_B(not_22_out), .LE2_B(or_2_out), .ADDRESS(PIXEL[2:0]), .Q0(six_11_q0),
    .Q1(six_11_q1), .Q2(six_11_q2), .Q4(six_11_q4), .Q5(six_11_q5), .Q6(six_11_q6));
  // RGBLED rgbled_19: pin names not known; wires that end beside it: six_11_q1, six_11_q0, six_11_q2
  six six_12 (
    .DATA(comparator_1_gt), .LE1_B(not_26_out), .LE2_B(or_2_out), .ADDRESS(PIXEL[2:0]), .Q0(six_12_q0),
    .Q1(six_12_q1), .Q2(six_12_q2), .Q4(six_12_q4), .Q5(six_12_q5), .Q6(six_12_q6));
  // RGBLED rgbled_20: pin names not known; wires that end beside it: six_12_q1, six_12_q0, six_12_q2
  six six_13 (
    .DATA(comparator_1_gt), .LE1_B(not_30_out), .LE2_B(or_2_out), .ADDRESS(PIXEL[2:0]), .Q0(six_13_q0),
    .Q1(six_13_q1), .Q2(six_13_q2), .Q4(six_13_q4), .Q5(six_13_q5), .Q6(six_13_q6));
  // RGBLED rgbled_21: pin names not known; wires that end beside it: six_13_q1, six_13_q0, six_13_q2
  six six_14 (
    .DATA(comparator_1_gt), .LE1_B(not_34_out), .LE2_B(or_2_out), .ADDRESS(PIXEL[2:0]), .Q0(six_14_q0),
    .Q1(six_14_q1), .Q2(six_14_q2), .Q4(six_14_q4), .Q5(six_14_q5), .Q6(six_14_q6));
  // RGBLED rgbled_22: pin names not known; wires that end beside it: six_14_q1, six_14_q0, six_14_q2
  six six_15 (
    .DATA(comparator_1_gt), .LE1_B(not_38_out), .LE2_B(or_2_out), .ADDRESS(PIXEL[2:0]), .Q0(six_15_q0),
    .Q1(six_15_q1), .Q2(six_15_q2), .Q4(six_15_q4), .Q5(six_15_q5), .Q6(six_15_q6));
  // RGBLED rgbled_23: pin names not known; wires that end beside it: six_15_q1, six_15_q0, six_15_q2
  six six_16 (
    .DATA(comparator_1_gt), .LE1_B(not_42_out), .LE2_B(or_2_out), .ADDRESS(PIXEL[2:0]), .Q0(six_16_q0),
    .Q1(six_16_q1), .Q2(six_16_q2), .Q4(six_16_q4), .Q5(six_16_q5), .Q6(six_16_q6));
  // RGBLED rgbled_24: pin names not known; wires that end beside it: six_16_q1, six_16_q0, six_16_q2
  // RGBLED rgbled_25: pin names not known; wires that end beside it: six_9_q5, six_9_q4, six_9_q6
  // RGBLED rgbled_26: pin names not known; wires that end beside it: six_10_q5, six_10_q4, six_10_q6
  // RGBLED rgbled_27: pin names not known; wires that end beside it: six_11_q5, six_11_q4, six_11_q6
  // RGBLED rgbled_28: pin names not known; wires that end beside it: six_12_q5, six_12_q4, six_12_q6
  // RGBLED rgbled_29: pin names not known; wires that end beside it: six_13_q5, six_13_q4, six_13_q6
  // RGBLED rgbled_30: pin names not known; wires that end beside it: six_14_q5, six_14_q4, six_14_q6
  // RGBLED rgbled_31: pin names not known; wires that end beside it: six_15_q5, six_15_q4, six_15_q6
  // RGBLED rgbled_32: pin names not known; wires that end beside it: six_16_q5, six_16_q4, six_16_q6
  six six_17 (
    .DATA(comparator_1_gt), .LE1_B(not_15_out), .LE2_B(or_2_out), .ADDRESS(PIXEL[2:0]), .Q0(six_17_q0),
    .Q1(six_17_q1), .Q2(six_17_q2), .Q4(six_17_q4), .Q5(six_17_q5), .Q6(six_17_q6));
  six six_18 (
    .DATA(comparator_1_gt), .LE1_B(not_19_out), .LE2_B(or_2_out), .ADDRESS(PIXEL[2:0]), .Q0(six_18_q0),
    .Q1(six_18_q1), .Q2(six_18_q2), .Q4(six_18_q4), .Q5(six_18_q5), .Q6(six_18_q6));
  six six_19 (
    .DATA(comparator_1_gt), .LE1_B(not_23_out), .LE2_B(or_2_out), .ADDRESS(PIXEL[2:0]), .Q0(six_19_q0),
    .Q1(six_19_q1), .Q2(six_19_q2), .Q4(six_19_q4), .Q5(six_19_q5), .Q6(six_19_q6));
  six six_20 (
    .DATA(comparator_1_gt), .LE1_B(not_27_out), .LE2_B(or_2_out), .ADDRESS(PIXEL[2:0]), .Q0(six_20_q0),
    .Q1(six_20_q1), .Q2(six_20_q2), .Q4(six_20_q4), .Q5(six_20_q5), .Q6(six_20_q6));
  six six_21 (
    .DATA(comparator_1_gt), .LE1_B(not_31_out), .LE2_B(or_2_out), .ADDRESS(PIXEL[2:0]), .Q0(six_21_q0),
    .Q1(six_21_q1), .Q2(six_21_q2), .Q4(six_21_q4), .Q5(six_21_q5), .Q6(six_21_q6));
  six six_22 (
    .DATA(comparator_1_gt), .LE1_B(not_35_out), .LE2_B(or_2_out), .ADDRESS(PIXEL[2:0]), .Q0(six_22_q0),
    .Q1(six_22_q1), .Q2(six_22_q2), .Q4(six_22_q4), .Q5(six_22_q5), .Q6(six_22_q6));
  six six_23 (
    .DATA(comparator_1_gt), .LE1_B(not_39_out), .LE2_B(or_2_out), .ADDRESS(PIXEL[2:0]), .Q0(six_23_q0),
    .Q1(six_23_q1), .Q2(six_23_q2), .Q4(six_23_q4), .Q5(six_23_q5), .Q6(six_23_q6));
  six six_24 (
    .DATA(comparator_1_gt), .LE1_B(not_43_out), .LE2_B(or_2_out), .ADDRESS(PIXEL[2:0]), .Q0(six_24_q0),
    .Q1(six_24_q1), .Q2(six_24_q2), .Q4(six_24_q4), .Q5(six_24_q5), .Q6(six_24_q6));
  // RGBLED rgbled_33: pin names not known; wires that end beside it: six_17_q1, six_17_q0, six_17_q2
  // RGBLED rgbled_34: pin names not known; wires that end beside it: six_17_q5, six_17_q4, six_17_q6
  // RGBLED rgbled_35: pin names not known; wires that end beside it: six_18_q1, six_18_q0, six_18_q2
  // RGBLED rgbled_36: pin names not known; wires that end beside it: six_18_q5, six_18_q4, six_18_q6
  // RGBLED rgbled_37: pin names not known; wires that end beside it: six_19_q1, six_19_q0, six_19_q2
  // RGBLED rgbled_38: pin names not known; wires that end beside it: six_19_q5, six_19_q4, six_19_q6
  // RGBLED rgbled_39: pin names not known; wires that end beside it: six_20_q1, six_20_q0, six_20_q2
  // RGBLED rgbled_40: pin names not known; wires that end beside it: six_20_q5, six_20_q4, six_20_q6
  // RGBLED rgbled_41: pin names not known; wires that end beside it: six_21_q1, six_21_q0, six_21_q2
  // RGBLED rgbled_42: pin names not known; wires that end beside it: six_21_q5, six_21_q4, six_21_q6
  // RGBLED rgbled_43: pin names not known; wires that end beside it: six_22_q1, six_22_q0, six_22_q2
  // RGBLED rgbled_44: pin names not known; wires that end beside it: six_22_q5, six_22_q4, six_22_q6
  // RGBLED rgbled_45: pin names not known; wires that end beside it: six_23_q1, six_23_q0, six_23_q2
  // RGBLED rgbled_46: pin names not known; wires that end beside it: six_23_q5, six_23_q4, six_23_q6
  // RGBLED rgbled_47: pin names not known; wires that end beside it: six_24_q1, six_24_q0, six_24_q2
  // RGBLED rgbled_48: pin names not known; wires that end beside it: six_24_q5, six_24_q4, six_24_q6
  six six_25 (
    .DATA(comparator_1_gt), .LE1_B(not_16_out), .LE2_B(or_2_out), .ADDRESS(PIXEL[2:0]), .Q0(six_25_q0),
    .Q1(six_25_q1), .Q2(six_25_q2), .Q4(six_25_q4), .Q5(six_25_q5), .Q6(six_25_q6));
  // RGBLED rgbled_49: pin names not known; wires that end beside it: six_25_q1, six_25_q0, six_25_q2
  six six_26 (
    .DATA(comparator_1_gt), .LE1_B(not_20_out), .LE2_B(or_2_out), .ADDRESS(PIXEL[2:0]), .Q0(six_26_q0),
    .Q1(six_26_q1), .Q2(six_26_q2), .Q4(six_26_q4), .Q5(six_26_q5), .Q6(six_26_q6));
  // RGBLED rgbled_50: pin names not known; wires that end beside it: six_26_q1, six_26_q0, six_26_q2
  six six_27 (
    .DATA(comparator_1_gt), .LE1_B(not_24_out), .LE2_B(or_2_out), .ADDRESS(PIXEL[2:0]), .Q0(six_27_q0),
    .Q1(six_27_q1), .Q2(six_27_q2), .Q4(six_27_q4), .Q5(six_27_q5), .Q6(six_27_q6));
  // RGBLED rgbled_51: pin names not known; wires that end beside it: six_27_q1, six_27_q0, six_27_q2
  six six_28 (
    .DATA(comparator_1_gt), .LE1_B(not_28_out), .LE2_B(or_2_out), .ADDRESS(PIXEL[2:0]), .Q0(six_28_q0),
    .Q1(six_28_q1), .Q2(six_28_q2), .Q4(six_28_q4), .Q5(six_28_q5), .Q6(six_28_q6));
  // RGBLED rgbled_52: pin names not known; wires that end beside it: six_28_q1, six_28_q0, six_28_q2
  six six_29 (
    .DATA(comparator_1_gt), .LE1_B(not_32_out), .LE2_B(or_2_out), .ADDRESS(PIXEL[2:0]), .Q0(six_29_q0),
    .Q1(six_29_q1), .Q2(six_29_q2), .Q4(six_29_q4), .Q5(six_29_q5), .Q6(six_29_q6));
  // RGBLED rgbled_53: pin names not known; wires that end beside it: six_29_q1, six_29_q0, six_29_q2
  six six_30 (
    .DATA(comparator_1_gt), .LE1_B(not_36_out), .LE2_B(or_2_out), .ADDRESS(PIXEL[2:0]), .Q0(six_30_q0),
    .Q1(six_30_q1), .Q2(six_30_q2), .Q4(six_30_q4), .Q5(six_30_q5), .Q6(six_30_q6));
  // RGBLED rgbled_54: pin names not known; wires that end beside it: six_30_q1, six_30_q0, six_30_q2
  six six_31 (
    .DATA(comparator_1_gt), .LE1_B(not_40_out), .LE2_B(or_2_out), .ADDRESS(PIXEL[2:0]), .Q0(six_31_q0),
    .Q1(six_31_q1), .Q2(six_31_q2), .Q4(six_31_q4), .Q5(six_31_q5), .Q6(six_31_q6));
  // RGBLED rgbled_55: pin names not known; wires that end beside it: six_31_q1, six_31_q0, six_31_q2
  six six_32 (
    .DATA(comparator_1_gt), .LE1_B(not_44_out), .LE2_B(or_2_out), .ADDRESS(PIXEL[2:0]), .Q0(six_32_q0),
    .Q1(six_32_q1), .Q2(six_32_q2), .Q4(six_32_q4), .Q5(six_32_q5), .Q6(six_32_q6));
  // RGBLED rgbled_56: pin names not known; wires that end beside it: six_32_q1, six_32_q0, six_32_q2
  // RGBLED rgbled_57: pin names not known; wires that end beside it: six_25_q5, six_25_q4, six_25_q6
  // RGBLED rgbled_58: pin names not known; wires that end beside it: six_26_q5, six_26_q4, six_26_q6
  // RGBLED rgbled_59: pin names not known; wires that end beside it: six_27_q5, six_27_q4, six_27_q6
  // RGBLED rgbled_60: pin names not known; wires that end beside it: six_28_q5, six_28_q4, six_28_q6
  // RGBLED rgbled_61: pin names not known; wires that end beside it: six_29_q5, six_29_q4, six_29_q6
  // RGBLED rgbled_62: pin names not known; wires that end beside it: six_30_q5, six_30_q4, six_30_q6
  // RGBLED rgbled_63: pin names not known; wires that end beside it: six_31_q5, six_31_q4, six_31_q6
  // RGBLED rgbled_64: pin names not known; wires that end beside it: six_32_q5, six_32_q4, six_32_q6

  // Notes on the sheet:
  //   contents of RGB_24_Bit_Colour (hex, n*v repeats v):
  //   ff 11 80 0 40 20 0 0 ff 3c 5 0 80 90 a0 0 9 fb 56 0 0 c0 1 0 2 3 4 0 aa ff ff 0 0 0 63 0 b8 89 e2 0
  //   23 2e 2c 0 99 33 62 173*0 35 24 df 5*0 aa bb cc
endmodule

module six (
  input  DATA,
  input  LE1_B,
  input  LE2_B,
  input  [2:0] ADDRESS,
  output Q0,
  output Q1,
  output Q2,
  output Q4,
  output Q5,
  output Q6
);

  wire decoder_1_out0, decoder_1_out1, decoder_1_out2, decoder_1_out4, decoder_1_out5, decoder_1_out6,
       not_1_out, or_1_out;

  or or_1 (or_1_out, LE1_B, LE2_B);
  not not_1 (not_1_out, or_1_out);
  Decoder #(.select(3)) decoder_1 (
    .out0(decoder_1_out0), .out1(decoder_1_out1), .out2(decoder_1_out2), .out4(decoder_1_out4),
    .out5(decoder_1_out5), .out6(decoder_1_out6), .sel(ADDRESS), .en(not_1_out));  // open: out3, out7
  D_Flip_Flop #(.trigger("high")) d_ff_1 (.clk(decoder_1_out0), .D(DATA), .Q(Q0));  // open: Qn, preset, reset
  D_Flip_Flop #(.trigger("high")) d_ff_2 (.clk(decoder_1_out1), .D(DATA), .Q(Q1));  // open: Qn, preset, reset
  D_Flip_Flop #(.trigger("high")) d_ff_3 (.clk(decoder_1_out2), .D(DATA), .Q(Q2));  // open: Qn, preset, reset
  D_Flip_Flop #(.trigger("high")) d_ff_4 (.clk(decoder_1_out4), .D(DATA), .Q(Q4));  // open: Qn, preset, reset
  D_Flip_Flop #(.trigger("high")) d_ff_5 (.clk(decoder_1_out5), .D(DATA), .Q(Q5));  // open: Qn, preset, reset
  D_Flip_Flop #(.trigger("high")) d_ff_6 (.clk(decoder_1_out6), .D(DATA), .Q(Q6));  // open: Qn, preset, reset
endmodule
