// Logisim project 658_CPU_Evolution.circ as structural Verilog: 5 circuits, main circuit Memory_Copier
module CPU_Board (
  input  INT0,
  input  INT1,
  input  INT2,
  input  INT3,
  input  INT4,
  input  INT5,
  input  INT6,
  input  INT7,
  output ExternalDeviceValid
);

  wire Address128K, AddressStage, AddressStageB, AddressValid, and_1_out, and_3_out, and_5_out, and_6_out,
       and_7_out, and_8_out, and_9_out, and_13_out, BALatch, BALatchB, Clock31MHz, Clock62MHz, Clock125MHz,
       clock_1_out, DataLatchB, decoder_1_out0, decoder_1_out1, decoder_1_out2, decoder_1_out3,
       decoder_1_out4, decoder_1_out5, decoder_1_out6, decoder_1_out7, DeviceValid, IDV, IRQ, IRQB,
       not_1_out, not_3_out, not_4_out, not_5_out, not_6_out, not_7_out, not_8_out, not_9_out, not_10_out,
       not_11_out, not_12_out, not_14_out, not_15_out, not_17_out, not_24_out, not_25_out, not_26_out,
       not_28_out, not_29_out, not_31_out, or_2_out, or_3_out, or_4_out, or_5_out, or_6_out, or_7_out,
       pull_resistor_1_node, Read, ReadB, undriven, VDA, VPA, VPB;
  wire [3:1] priority_encoder_1_out;
  wire [3:3] counter_1_q;
  wire [7:0] BA_Latch_q, BA_Latch_t, DBA, latch8bit3state_1_t, transceiver8bit_1_q, transceiver8bit_4_q;
  wire [15:0] A;

  // Probe on BA_Latch_t
  Latch8bit3State BA_Latch (.T(BA_Latch_t), .Q(BA_Latch_q), .D(DBA), .LE(BALatch), .OEB(pull_resistor_1_node));
  Pull_Resistor pull_resistor_1 (.node(pull_resistor_1_node));
  // W65C816S w65c816s_1: pin names not known; wires that end beside it: AddressStage, A, DBA
  not not_1 (not_1_out, VPB);
  and and_1 (and_1_out, not_1_out, A[3], A[2], A[1]);
  and and_2 (IRQ, undriven, and_1_out);
  not not_2 (IRQB, undriven);
  Priority_Encoder priority_encoder_1 (
    .in0(INT0), .in1(INT1), .in2(INT2), .in3(INT3), .in4(INT4), .in5(INT5), .in6(INT6), .in7(INT7),
    .out(priority_encoder_1_out));  // open: en_in
  and and_3 (and_3_out, not_4_out, not_5_out, not_6_out);
  and and_4 (Address128K, and_3_out, and_6_out);
  not not_3 (not_3_out, BA_Latch_q[0]);
  not not_4 (not_4_out, BA_Latch_q[1]);
  not not_5 (not_5_out, BA_Latch_q[2]);
  not not_6 (not_6_out, BA_Latch_q[3]);
  not not_7 (not_7_out, BA_Latch_q[4]);
  not not_8 (not_8_out, BA_Latch_q[5]);
  not not_9 (not_9_out, BA_Latch_q[6]);
  and and_5 (and_5_out, not_3_out, not_4_out, not_5_out, not_6_out);
  and and_6 (and_6_out, not_7_out, not_8_out, not_9_out, not_10_out);
  and and_7 (and_7_out, and_5_out, and_6_out);
  not not_10 (not_10_out, BA_Latch_q[7]);
  not not_11 (not_11_out, A[8]);
  and and_8 (and_8_out, A[15], A[14], A[13], A[12]);
  and and_9 (and_9_out, A[11], A[10], A[9], not_11_out);
  and and_10 (DeviceValid, and_8_out, and_9_out);
  or or_1 (AddressValid, VDA, VPA);
  and and_11 (IDV, DeviceValid, A[7], and_7_out);
  not not_12 (not_12_out, A[7]);
  not not_13 (ReadB, Read);
  // Probe on A[3:0]
  // Probe on A[7:4]
  and and_12 (ExternalDeviceValid, DeviceValid, not_12_out, and_7_out);
  Transceiver8bit transceiver8bit_1 (.Q(transceiver8bit_1_q), .D(A[15:8]), .OEB(IRQ));
  Transceiver8bit transceiver8bit_2 (
    .Q(transceiver8bit_1_q), .D({4'b0000, priority_encoder_1_out, A[0]}), .OEB(not_14_out));
  // Probe on {4'b0000, priority_encoder_1_out, A[0]}
  not not_14 (not_14_out, IRQ);
  or or_2 (or_2_out, AddressStage, ReadB);
  // Probe on nothing
  // Probe on DBA
  // Probe on A[6:4]
  Decoder #(.enable("false"), .select(3)) decoder_1 (
    .out0(decoder_1_out0), .out1(decoder_1_out1), .out2(decoder_1_out2), .out3(decoder_1_out3),
    .out4(decoder_1_out4), .out5(decoder_1_out5), .out6(decoder_1_out6), .out7(decoder_1_out7), .sel(A[6:4]));
  not not_15 (not_15_out, decoder_1_out0);
  // NOT_Gate not_16 has open pins: in=decoder_1_out1, out=open
  not not_17 (not_17_out, IDV);
  or or_3 (or_3_out, AddressStageB, ReadB);
  or or_4 (or_4_out, or_3_out, not_17_out, not_15_out);
  // Probe on latch8bit3state_1_t
  Latch8bit3State latch8bit3state_1 (.T(latch8bit3state_1_t), .Q(DBA), .D(DBA), .LE(not_25_out), .OEB(or_4_out));
  or or_5 (or_5_out, AddressStage, Read);
  // Probe on transceiver8bit_4_q
  Transceiver8bit transceiver8bit_3 (.Q(DBA), .D(transceiver8bit_4_q), .OEB(or_2_out));
  // Probe on nothing
  Transceiver8bit transceiver8bit_4 (.Q(transceiver8bit_4_q), .D(DBA), .OEB(or_5_out));
  // NOT_Gate not_18 has open pins: in=decoder_1_out2, out=open
  // NOT_Gate not_19 has open pins: in=decoder_1_out3, out=open
  // NOT_Gate not_20 has open pins: in=decoder_1_out4, out=open
  // NOT_Gate not_21 has open pins: in=decoder_1_out5, out=open
  // NOT_Gate not_22 has open pins: in=decoder_1_out6, out=open
  // NOT_Gate not_23 has open pins: in=decoder_1_out7, out=open
  not not_24 (not_24_out, IDV);
  or or_6 (or_6_out, AddressStage, Read);
  or or_7 (or_7_out, not_15_out, not_24_out, or_6_out);
  not not_25 (not_25_out, or_7_out);
  // Probe on DBA
  not not_26 (not_26_out, clock_1_out);
  Counter #(.max('hf), .width(4)) counter_1 (
    .Q({counter_1_q[3], AddressStage, Clock31MHz, Clock62MHz}), .clk(clock_1_out));  // open: load, D, count, carry, up, clr
  Clock clock_1 (.out(clock_1_out));
  not not_27 (Clock125MHz, not_26_out);
  not not_28 (not_28_out, Clock62MHz);
  not not_29 (not_29_out, Clock31MHz);
  not not_30 (AddressStageB, AddressStage);
  or or_8 (BALatchB, AddressStageB, Clock31MHz, not_28_out);
  or or_9 (DataLatchB, AddressStage, Clock31MHz, Clock62MHz);
  not not_31 (not_31_out, DeviceValid);
  and and_13 (and_13_out, AddressValid, not_31_out, Address128K, AddressStageB);
  RAM #(.addrWidth(17), .databus("bidir"), .trigger("high"), .\type ("nonvolatile")) ram_1 (
    .addr({BA_Latch_q[0], transceiver8bit_1_q, A[7:0]}), .we(Read), .oe(and_13_out),
    .data(transceiver8bit_4_q));  // open: clk
  // Probe on {BA_Latch_q[0], transceiver8bit_1_q, A[7:0]}

  // Other names for the same wires on the sheet: Clock16MHz = AddressStage; DataStageB = AddressStage;
  //   PHI2 = AddressStage; DataStage = AddressStageB; Write = ReadB; RWB = Read; WriteB = Read

  // Notes on the sheet:
  //   Bank Address
  //   In 64K Address
  //   Internal Device Valid
  //   Device Address
  //   Device ID
endmodule

module Memory_Copier (
  input  Copy_ROM,
  input  Copy_Latch,
  input  ABORT,
  input  Write,
  input  D0,
  input  D1,
  input  D2,
  input  D3,
  input  D4,
  input  D5,
  input  D6,
  input  D7
);

  wire and_1_out, Clk_out, controlled_buffer_1_out, controlled_buffer_2_out, controlled_buffer_3_out,
       counter_1_carry, counter_2_carry, d_ff_1_q, d_ff_2_q, not_1_out, not_2_out, or_1_out, or_2_out,
       or_3_out, pull_resistor_1_node, pull_resistor_2_node, pull_resistor_3_node, pull_resistor_4_node,
       pull_resistor_5_node;
  wire [3:0] counter_2_q;
  wire [7:0] controlled_buffer_4_out, register_1_q, rom_1_data;
  wire [11:0] counter_1_q;

  Clock Clk (.out(Clk_out));
  assign controlled_buffer_1_out = pull_resistor_1_node ? Copy_ROM : 1'bz;  // Controlled_Buffer controlled_buffer_1
  Pull_Resistor #(.pull(1)) pull_resistor_1 (.node(pull_resistor_1_node));
  assign controlled_buffer_2_out = pull_resistor_2_node ? Copy_Latch : 1'bz;  // Controlled_Buffer controlled_buffer_2
  Pull_Resistor #(.pull(1)) pull_resistor_2 (.node(pull_resistor_2_node));
  assign controlled_buffer_3_out = pull_resistor_3_node ? ABORT : 1'bz;  // Controlled_Buffer controlled_buffer_3
  Pull_Resistor #(.pull(1)) pull_resistor_3 (.node(pull_resistor_3_node));
  not not_1 (not_1_out, Write);
  or or_1 (or_1_out, controlled_buffer_1_out, controlled_buffer_2_out, controlled_buffer_3_out, or_3_out);
  D_Flip_Flop #(.trigger("high")) d_ff_1 (
    .clk(controlled_buffer_1_out), .D(controlled_buffer_1_out), .Q(d_ff_1_q), .reset(or_3_out));  // open: Qn, preset
  D_Flip_Flop #(.trigger("high")) d_ff_2 (
    .clk(controlled_buffer_2_out), .D(controlled_buffer_2_out), .Q(d_ff_2_q), .reset(or_3_out));  // open: Qn, preset
  not not_2 (not_2_out, or_1_out);
  or or_2 (or_2_out, d_ff_1_q, d_ff_2_q);
  or or_3 (or_3_out, counter_2_carry, controlled_buffer_3_out);
  Register #(.trigger("high")) register_1 (
    .D({D7, D6, D5, D4, D3, D2, D1, D0}), .en(not_1_out), .Q(register_1_q), .clk(not_1_out));  // open: clr
  and and_1 (and_1_out, Clk_out, not_2_out, or_2_out);
  Counter #(.max('hfff), .width(12)) counter_1 (
    .Q(counter_1_q), .carry(counter_1_carry), .clk(and_1_out), .clr(or_1_out));  // open: load, D, count, up
  Counter #(.max('hf), .width(4)) counter_2 (
    .Q(counter_2_q), .carry(counter_2_carry), .clk(counter_1_carry), .clr(or_1_out));  // open: load, D, count, up
  ROM #(.addrWidth(16)) rom_1 (.addr({counter_2_q, counter_1_q}), .data(rom_1_data));
  assign controlled_buffer_4_out = d_ff_1_q ? rom_1_data : 8'bz;  // Controlled_Buffer controlled_buffer_4
  assign controlled_buffer_4_out = d_ff_2_q ? register_1_q : 8'bz;  // Controlled_Buffer controlled_buffer_5
  Pull_Resistor pull_resistor_4 (.node(pull_resistor_4_node));
  // Probe on {counter_2_q, counter_1_q}
  RAM #(.addrWidth(16), .databus("bidir"), .enables("line"), .trigger("high")) ram_1 (
    .addr({counter_2_q, counter_1_q}), .data(controlled_buffer_4_out));  // open: we, oe, clk
  Pull_Resistor #(.pull(1)) pull_resistor_5 (.node(pull_resistor_5_node));
  // Probe on controlled_buffer_4_out

  // Notes on the sheet:
  //   contents of rom_1 (hex, n*v repeats v):
  //   40 9c c3 1a 7e b9 ef f3 b6 16 c2 83 d7 11 dd f2 85 ad b6 ac 57 d0 d7 a1 18 84 1b 86 7 38 f6 14 19 fd
  //   ab 45 33 ca 94 9b 71 b9 5e 5a 63 49 4c ca 4c 9b 70 77 62 b6 f6 72 12 c4 5b 8e 3a 54 af a5 6e 97 d7
  //   d1 35 a4 ce b4 4a b5 e0 b2 dc 69 ef 33 d0 1 af e4 fb a5 eb f3 69 9d bf 57 9a 99 dc 6 c0 ea c9 3e 4
  //   c7 1d bf c0 8b c7 c c3 f3 47 ae 90 61 f3 71 a0 1c 35 a6 9d 8f c8 61 a7 87 ff b9 90 76 ff c 20 b4 1
  //   3a 52 b9 93 e6 96 65 d5 b9 e 3a bc a0 d3 9d 53 a 2e 1a f6 2b e0 9e 97 3d 5c bb fb bb 9 e9 fa a6 82
  //   c1 c3 c1 d6 41 17 d5 c9 b 8a ef 12 a7 c7 9e 9d be ca 37 c7 5e 24 12 a6 3a 3b cb 3f e7 88 83 cf 21 d9
  //   1d 4 5 8e 83 41 56 dd df df ba f e4 68 fb c2 4 db 47 26 b8 ec 71 41 bc 42 2e 2c 51 b8 5a 54 7a 9e 33
  //   bb 41 f6 9a 35 f1 b8 55 ad 5a 10 50 5f 11 9c d9 1d af af e1 8b e 92 3f 64 90 bf ed b4 59 25 49 1c 90
  //   68 56 12 a3 1f fa 20 82 15 3f 21 e0 8a 94 89 76 70 a 9b 41 af 98 b1 c0 62 58 78 38 19 c9 32 f1 17 c
  //   f4 77 92 28 e7 da f7 47 89 f0 24 f8 e9 8f ad 6c ef d5 19 ba 93 61 23 1c 22 98 fb 31 7e e2 83 3a 5b
  //   eb 93 5f 84 e4 36 e8 15 c0 ec 85 bf 79 e8 87 9 4a 50 25 8a f3 81 ba 31 f9 49 3 7e e4 2c 62 c7 81 a1
  //   1e 75 1f 53 a2 46 d2 61 bb 8a b4 9f db 67 20 d4 5a 16 f6 fb b0 24 db 84 bd b3 78 92 3 b8 b7 3b e7 3c
  //   a cc f5 9c a5 3 1a ca c0 54 e8 8b d7 25 d7 b7 ea 13 80 7d bf 2d e1 9e 1c 35 9c ae f e3 39 58 27 22
  //   61 97 b9 52 22 ff 1c 85 2f f3 ef c3 1d ed 4f 48 a8 bb 23 c2 ed bd 51 95 af 29 7 17 94 48 f4 d5 66 b8
  //   8d cd 53 a9 4a b3 2e 20 e8 2e ac 38 a5 19 a9 5e 88 c4 63 91 98 31 bb a9 20 59 77 8e f3 65 83 7d a3
  //   f6 2d 47 c9 5f 66 93 42 e6 5 18 6c 8 4 e5 6e b3 c1 9b 6f 8b 3f ae db 27 64 a8 a2 52 3a 67 7a 4c 30
  //   5b 19 7 57 ca 7c 6b a6 e 25 94 37 d2 55 10 89 59 57 22 bd b8 b6 3 da 18 83 1d a f6 91 4f dc 64 ba 2d
  //   81 47 18 3d 10 98 4e 3c c4 a4 be 59 39 4d d1 76 b4 47 33 6b 59 5d 14 44 73 ab 6a 7e b1 e2 2c 4f 64
  //   88 95 dc c4 37 68 82 29 db 27 f 53 f5 5b 7 a3 db d0 e1 61 f6 d7 48 f5 4 84 5b 2f 55 ee ee 80 f 73 c9
  //   40 6b f3 e5 e7 f6 11 b3 55 d2 76 55 c f4 f e3 71 65 4b a9 10 82 5e 65 d6 3d 82 8b 56 5a 32 82 5 b4
  //   6f e4 7f 77 fc c3 c1 65 a2 e0 6d 12 6e f3 b 28 ef e7 44 a5 7a 1c 26 1a 67 a4 64 eb 52 88 93 92 5c 1
  //   6f dd 68 c0 15 2c 60 28 48 b5 6f 8f ae c1 45 82 11 ed 57 0 9f 6b 1d bb 2b 40 53 5b 6b 85 3a bb 38 a7
  //   d6 2a d3 a8 2e ad 1c 5d 90 39 da af cb fb f7 db 74 90 c1 b2 24 4e 2b db b5 7b b d 89 91 5b 57 c4 82
  //   79 5a 8d ef 68 8a 52 70 e 71 3 d0 75 ed 53 4e c 6e fb de e4 3a f8 68 f4 aa c9 5 56 6c b3 46 89 c0 fe
  //   6e ae bc 36 b3 cc 89 6b 82 d a4 73 b9 0 1f 24 ec d6 df 9c a2 a6 dd 7a 96 ab 66 23 f7 81 5b ff a9 6d
  //   73 ba 84 93 75 85 91 3e 80 54 51 1d 45 1e f6 81 48 21 a9 a2 24 1c c3 d8 c4 94 16 e3 ac 11 22 24 2f
  //   60 61 e3 b7 d0 7d 88 2 75 96 e3 60 69 7e 65 f7 7 fd 66 0 2f e 5e 8 86 21 2d 31 b5 58 55 70 a6 cc 3b
  //   ce cb c6 6b a8 58 7 d2 f0 85 2 3 6a ce 1e 73 f1 33 f6 be b1 7a 99 e1 6b 69 cb 7f b6 e 43 1d 39 f8 ec
  //   67 f3 7c 26 6a 74 f2 4 d9 23 f6 8c 49 77 a8 fa 76 3f ee fe 7d db ae fb 21 81 16 48 8 7a d5 70 fc 63
  //   60 72 2b 6e 2f 2 68 a0 ff c7 69 12 f 9c 8 31 63 d1 83 ff 5 68 bd 51 40 59 7c f e4 d0 aa 78 86 6b 95
  //   5d be 7d 30 63 69 4f 51 42 e6 5b f2 9 59 90 71 58 ec 92 d1 a6 a f8 f8 7a a3 8d f0 b3 6d 91 28 c1 1e
  //   f6 b1 ea b4 a4 82 87 ae b6 b5 46 50 bc c9 67 e4 f9 df 0 f5 a3 fe 3a 94 27 50 92 94 63 64 1a cf eb 6b
  //   b7 60 46 7c 61 e7 2f d2 67 c9 d6 9 aa 6e 1d 66 df 82 dc d ce 36 1e 49 96 7d 63 c9 e8 51 de de 48 ec
  //   b5 c0 50 11 45 c7 ee 42 5c b3 a2 8 7e e5 c3 2f 21 a5 b8 8 f2 5b 3f a7 10 d7 ab 23 4d 8a 1e da 71 cc
  //   d5 ac 77 15 5a 3c cf 45 d0 33 9c de 2c 7e f4 45 76 8c 24 6 e 92 ea e e2 c7 b9 f0 ba a9 fa 21 6e 38
  //   47 3d 2b 37 af 41 b2 70 f7 d0 9a ed d4 6f 8a 40 32 ca 81 bd 70 ee f bc a3 8e 9a d9 d0 3f 9c 35 34 bd
  //   e0 b3 7d 25 ca 3d e 3a 8d fe 40 a2 73 a6 9d 27 19 aa 24 f7 b1 82 89 e5 40 ea 73 a7 df 23 bd 17 fb 31
  //   b7 73 96 1b 63 9e 85 2f ba 5e b0 3c e5 9d 56 d8 85 a9 48 99 ed 75 2a 5c 63 d7 b7 82 64 c9 fb 2f de
  //   a9 97 8b 75 7a 2 2 c0 22 c3 84 8a ac b9 c6 13 84 54 81 4d be da af 20 50 a4 d2 a8 54 60 2e 73 49 4e
  //   b c4 50 83 f5 d4 70 2a fd c d3 c0 f6 4e 8 55 b9 2b 40 ce 63 2a 92 26 93 8 39 a9 ae f4 d1 39 1c d0 9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
endmodule

module Latch8bit3State (
  input  [7:0] D,
  input  LE,
  input  OEB,
  output [7:0] T,
  output [7:0] Q
);

  wire not_1_out, pull_resistor_1_node;

  Pull_Resistor #(.pull(1)) pull_resistor_1 (.node(pull_resistor_1_node));
  assign Q = not_1_out ? T : 8'bz;  // Controlled_Buffer controlled_buffer_1
  Register #(.trigger("high")) register_1 (.D(D), .en(pull_resistor_1_node), .Q(T), .clk(LE));  // open: clr
  not not_1 (not_1_out, OEB);
endmodule

module Transceiver8bit (
  input  [7:0] D,
  input  OEB,
  output [7:0] Q
);

  wire not_1_out;

  assign Q = not_1_out ? D : 8'bz;  // Controlled_Buffer controlled_buffer_1
  not not_1 (not_1_out, OEB);
endmodule

module Range_Test (
  input  [2:0] MIN,
  input  [2:0] D,
  input  [2:0] MAX,
  output out_4
);

  wire comparator_1_eq, comparator_1_gt, comparator_2_eq, comparator_2_lt, or_1_out, or_2_out;

  Comparator #(.mode("unsigned"), .width(3)) comparator_1 (
    .a(D), .b(MIN), .gt(comparator_1_gt), .eq(comparator_1_eq));  // open: lt
  Comparator #(.mode("unsigned"), .width(3)) comparator_2 (
    .a(D), .b(MAX), .eq(comparator_2_eq), .lt(comparator_2_lt));  // open: gt
  or or_1 (or_1_out, comparator_1_gt, comparator_1_eq);
  or or_2 (or_2_out, comparator_2_eq, comparator_2_lt);
  and and_1 (out_4, or_1_out, or_2_out);
endmodule
