// Logisim project Address Decode.circ as structural Verilog: 8 circuits, main circuit CPU Board
module CPU_Board (
  input  in_1,
  input  in_2,
  input  in_3,
  input  in_4,
  input  in_5,
  input  in_6,
  input  in_7,
  input  in_8,
  input  in_9,
  input  in_10,
  input  in_11,
  input  in_12,
  input  in_13,
  input  in_14,
  input  in_15,
  input  in_16
);

  wire interrupt_decode_1_int, interrupt_latch_1_irqb, interrupt_latch_1_nmib, interrupt_select_1_irq,
       interrupt_select_1_nmi, not_1_out, PHI2, pull_resistor_1_node, pull_resistor_3_node, w65c816s_1_da,
       w65c816s_1_pa, w65c816s_1_r_wb, w65c816s_1_vpb;
  wire [3:0] interrupt_decode_1_int_addr0;
  wire [6:0] interrupt_latch_1_lint_addr1;
  wire [7:0] controlled_buffer_1_out, controlled_buffer_2_out, pull_resistor_2_node, w65c816s_1_addr0,
       w65c816s_1_addr16, w65c816s_1_data7__w, w65c816s_1_ic;
  wire [15:0] multiplexer_1_out;

  Clock u_PHI2 (.out(PHI2));
  Pull_Resistor pull_resistor_1 (.node(pull_resistor_1_node));
  Pull_Resistor pull_resistor_2 (.node(pull_resistor_2_node));
  Pull_Resistor pull_resistor_3 (.node(pull_resistor_3_node));
  Interrupt_Select interrupt_select_1 (
    .INT_ADDR0(interrupt_decode_1_int_addr0[0]), .INT_ADDR1(interrupt_decode_1_int_addr0[1]),
    .INT_ADDR2(interrupt_decode_1_int_addr0[2]), .INT_ADDR3(interrupt_decode_1_int_addr0[3]),
    .INT(interrupt_decode_1_int), .Write(pull_resistor_1_node), .D0(pull_resistor_2_node[0]),
    .D1(pull_resistor_2_node[1]), .D2(pull_resistor_2_node[2]), .D3(pull_resistor_2_node[3]),
    .D4(pull_resistor_2_node[4]), .D5(pull_resistor_2_node[5]), .D6(pull_resistor_2_node[6]),
    .D7(pull_resistor_2_node[7]), .NMI(interrupt_select_1_nmi), .IRQ(interrupt_select_1_irq));
  Interrupt_Decode interrupt_decode_1 (
    .INT0(in_1), .INT1(in_2), .INT2(in_3), .INT3(in_4), .INT4(in_5), .INT5(in_6), .INT6(in_7), .INT7(in_8),
    .INT8(in_9), .INT9(in_10), .INT10(in_11), .INT11(in_12), .INT12(in_13), .INT13(in_14), .INT14(in_15),
    .INT15(in_16), .VPB(pull_resistor_3_node), .INT_ADDR0(interrupt_decode_1_int_addr0[0]),
    .INT_ADDR1(interrupt_decode_1_int_addr0[1]), .INT_ADDR2(interrupt_decode_1_int_addr0[2]),
    .INT_ADDR3(interrupt_decode_1_int_addr0[3]), .INT(interrupt_decode_1_int));
  Interrupt_Latch interrupt_latch_1 (
    .PHI2(PHI2), .INT_ADDR0(interrupt_decode_1_int_addr0[3]), .INT_ADDR1(interrupt_decode_1_int_addr0[2]),
    .INT_ADDR2(interrupt_decode_1_int_addr0[1]), .INT_ADDR3(interrupt_decode_1_int_addr0[0]),
    .NMI(interrupt_select_1_nmi), .IRQ(interrupt_select_1_irq), .LINT_ADDR1(interrupt_latch_1_lint_addr1[0]),
    .LINT_ADDR2(interrupt_latch_1_lint_addr1[1]), .LINT_ADDR3(interrupt_latch_1_lint_addr1[2]),
    .LINT_ADDR4(interrupt_latch_1_lint_addr1[3]), .LINT_ADDR5(interrupt_latch_1_lint_addr1[4]),
    .LINT_ADDR6(interrupt_latch_1_lint_addr1[5]), .LINT_ADDR7(interrupt_latch_1_lint_addr1[6]),
    .IRQB(interrupt_latch_1_irqb), .NMIB(interrupt_latch_1_nmib), .INT(interrupt_decode_1_int));
  // Probe on {w65c816s_1_addr16, multiplexer_1_out[15:8], w65c816s_1_addr0}
  W65C816S w65c816s_1 (
    .PHI2(PHI2), .NMIB(interrupt_latch_1_nmib), .IRQB(interrupt_latch_1_irqb),
    .DATA0__R(controlled_buffer_1_out[7]), .DATA1__R(controlled_buffer_1_out[6]),
    .DATA2__R(controlled_buffer_1_out[5]), .DATA3__R(controlled_buffer_1_out[4]),
    .DATA4__R(controlled_buffer_1_out[3]), .DATA5__R(controlled_buffer_1_out[2]),
    .DATA6__R(controlled_buffer_1_out[1]), .DATA7__R(controlled_buffer_1_out[0]),
    .DATA0__W(w65c816s_1_data7__w[7]), .DATA1__W(w65c816s_1_data7__w[6]), .DATA2__W(w65c816s_1_data7__w[5]),
    .DATA3__W(w65c816s_1_data7__w[4]), .DATA4__W(w65c816s_1_data7__w[3]), .DATA5__W(w65c816s_1_data7__w[2]),
    .DATA6__W(w65c816s_1_data7__w[1]), .DATA7__W(w65c816s_1_data7__w[0]), .R_WB(w65c816s_1_r_wb),
    .ADDR0(w65c816s_1_addr0[0]), .ADDR1(w65c816s_1_addr0[1]), .ADDR2(w65c816s_1_addr0[2]),
    .ADDR3(w65c816s_1_addr0[3]), .ADDR4(w65c816s_1_addr0[4]), .ADDR5(w65c816s_1_addr0[5]),
    .ADDR6(w65c816s_1_addr0[6]), .ADDR7(w65c816s_1_addr0[7]), .ADDR8(multiplexer_1_out[8]),
    .ADDR9(multiplexer_1_out[9]), .ADDR10(multiplexer_1_out[10]), .ADDR11(multiplexer_1_out[11]),
    .ADDR12(multiplexer_1_out[12]), .ADDR13(multiplexer_1_out[13]), .ADDR14(multiplexer_1_out[14]),
    .ADDR15(multiplexer_1_out[15]), .ADDR16(w65c816s_1_addr16[0]), .ADDR17(w65c816s_1_addr16[1]),
    .ADDR18(w65c816s_1_addr16[2]), .ADDR19(w65c816s_1_addr16[3]), .ADDR20(w65c816s_1_addr16[4]),
    .ADDR21(w65c816s_1_addr16[5]), .ADDR22(w65c816s_1_addr16[6]), .ADDR23(w65c816s_1_addr16[7]),
    .DA(w65c816s_1_da), .PA(w65c816s_1_pa), .VPB(w65c816s_1_vpb), .IC(w65c816s_1_ic));
  Multiplexer #(.width(8)) multiplexer_1 (
    .in0({interrupt_latch_1_lint_addr1, w65c816s_1_addr0[0]}), .in1(w65c816s_1_addr0),
    .out(multiplexer_1_out[7:0]), .sel(w65c816s_1_vpb));  // open: en
  // Probe on w65c816s_1_ic
  assign controlled_buffer_1_out = w65c816s_1_r_wb ? controlled_buffer_2_out : 8'bz;  // Controlled_Buffer controlled_buffer_1
  not not_1 (not_1_out, w65c816s_1_r_wb);
  assign controlled_buffer_2_out = not_1_out ? w65c816s_1_data7__w : 8'bz;  // Controlled_Buffer controlled_buffer_2
  // Probe on controlled_buffer_2_out
  // Probe on multiplexer_1_out
  RAM #(.addrWidth(16)) ram_1 (
    .addr(multiplexer_1_out), .data(controlled_buffer_2_out), .ld(w65c816s_1_r_wb));  // open: sel, clk, clr

  // Notes on the sheet:
  //   Address         Bus
  //   IRQ B
  //   N MIB
  //   W65C816
  //   D A
  //   P A
  //   VP B
  //   R WB
  //   Data  Bus
endmodule

module W65C816S (
  input  DATA0__R,
  input  DATA1__R,
  input  DATA2__R,
  input  DATA3__R,
  input  DATA4__R,
  input  DATA5__R,
  input  DATA6__R,
  input  DATA7__R,
  input  PHI2,
  input  NMIB,
  input  IRQB,
  output DATA0__W,
  output DATA1__W,
  output DATA2__W,
  output DATA3__W,
  output DATA4__W,
  output DATA5__W,
  output DATA6__W,
  output DATA7__W,
  output R_WB,
  output ADDR0,
  output ADDR1,
  output ADDR2,
  output ADDR3,
  output ADDR4,
  output ADDR5,
  output ADDR6,
  output ADDR7,
  output ADDR8,
  output ADDR9,
  output ADDR10,
  output ADDR11,
  output ADDR12,
  output ADDR13,
  output ADDR14,
  output ADDR15,
  output ADDR16,
  output ADDR17,
  output ADDR18,
  output ADDR19,
  output ADDR20,
  output ADDR21,
  output ADDR22,
  output ADDR23,
  output DA,
  output PA,
  output VPB,
  output [7:0] IC
);

  wire and_1_out, and_2_out, and_3_out, and_4_out, and_5_out, counter_1_q, d_ff_1_q,
       mpu_int_emulation_1_busy, mpu_int_emulation_1_da, mpu_int_emulation_1_pa, mpu_int_emulation_1_r_wb,
       mpu_prg_emulation_1_busy, mpu_prg_emulation_1_da, mpu_prg_emulation_1_pa, mpu_prg_emulation_1_r_wb,
       not_1_out, not_2_out, not_3_out, not_4_out, not_5_out, or_1_out, or_2_out;
  wire [7:0] adder_1_out, controlled_buffer_9_out, mpu_int_emulation_1_data, mpu_int_emulation_1_ic,
       mpu_prg_emulation_1_data, mpu_prg_emulation_1_ic;
  wire [15:0] mpu_int_emulation_1_addr, mpu_prg_emulation_1_addr;

  Counter #(.width(1), .max('h1), .trigger("falling")) counter_1 (
    .Q(counter_1_q), .clk(mpu_prg_emulation_1_busy), .clr(mpu_prg_emulation_1_busy));  // open: load, D, count, carry
  or or_1 (or_1_out, counter_1_q, mpu_prg_emulation_1_busy);
  not not_1 (not_1_out, mpu_int_emulation_1_busy);
  and and_1 (and_1_out, or_1_out, not_1_out);
  not not_2 (not_2_out, and_1_out);
  and and_2 (and_2_out, NMIB, IRQB);
  not not_3 (not_3_out, mpu_prg_emulation_1_busy);
  D_Flip_Flop #(.trigger("high")) d_ff_1 (
    .clk(not_4_out), .D(not_4_out), .Q(d_ff_1_q), .reset(mpu_int_emulation_1_busy));  // open: Qn, preset, en
  not not_4 (not_4_out, and_2_out);
  and and_3 (and_3_out, not_3_out, d_ff_1_q);
  and and_4 (and_4_out, PHI2, mpu_int_emulation_1_busy);
  and and_5 (and_5_out, PHI2, not_5_out);
  not not_5 (not_5_out, mpu_int_emulation_1_busy);
  or or_2 (or_2_out, and_3_out, and_4_out);
  LED led_1 (.in(and_1_out));
  MPU_PRG_Emulation mpu_prg_emulation_1 (
    .PHI2(and_5_out), .DATA(mpu_prg_emulation_1_data), .R_WB(mpu_prg_emulation_1_r_wb),
    .ADDR(mpu_prg_emulation_1_addr), .DA(mpu_prg_emulation_1_da), .PA(mpu_prg_emulation_1_pa),
    .BUSY(mpu_prg_emulation_1_busy), .IC(mpu_prg_emulation_1_ic));
  // Probe on mpu_prg_emulation_1_ic
  LED led_2 (.in(not_2_out));
  MPU_INT_Emulation mpu_int_emulation_1 (
    .PHI2(or_2_out), .IRQB(NMIB), .NMIB(IRQB), .DATA(mpu_int_emulation_1_data),
    .BUSY(mpu_int_emulation_1_busy), .R_WB(mpu_int_emulation_1_r_wb), .ADDR(mpu_int_emulation_1_addr),
    .DA(mpu_int_emulation_1_da), .PA(mpu_int_emulation_1_pa), .VPB(VPB), .IC(mpu_int_emulation_1_ic));
  // Probe on mpu_int_emulation_1_ic
  Adder adder_1 (.a(mpu_int_emulation_1_ic), .b(8'h10), .out(adder_1_out), .cin(and_1_out));  // open: cout
  assign {DATA7__W, DATA6__W, DATA5__W, DATA4__W, DATA3__W, DATA2__W, DATA1__W, DATA0__W} = and_1_out ? mpu_prg_emulation_1_data : 8'bz;  // Controlled_Buffer controlled_buffer_1
  assign {DATA7__W, DATA6__W, DATA5__W, DATA4__W, DATA3__W, DATA2__W, DATA1__W, DATA0__W} = not_2_out ? mpu_int_emulation_1_data : 8'bz;  // Controlled_Buffer controlled_buffer_2
  assign R_WB = and_1_out ? mpu_prg_emulation_1_r_wb : 1'bz;  // Controlled_Buffer controlled_buffer_3
  assign R_WB = not_2_out ? mpu_int_emulation_1_r_wb : 1'bz;  // Controlled_Buffer controlled_buffer_4
  assign {ADDR15, ADDR14, ADDR13, ADDR12, ADDR11, ADDR10, ADDR9, ADDR8, ADDR7, ADDR6, ADDR5, ADDR4, ADDR3, ADDR2, ADDR1, ADDR0} = and_1_out ? mpu_prg_emulation_1_addr : 16'bz;  // Controlled_Buffer controlled_buffer_5
  assign {ADDR15, ADDR14, ADDR13, ADDR12, ADDR11, ADDR10, ADDR9, ADDR8, ADDR7, ADDR6, ADDR5, ADDR4, ADDR3, ADDR2, ADDR1, ADDR0} = not_2_out ? mpu_int_emulation_1_addr : 16'bz;  // Controlled_Buffer controlled_buffer_6
  assign IC = and_1_out ? mpu_prg_emulation_1_ic : 8'bz;  // Controlled_Buffer controlled_buffer_7
  assign IC = not_2_out ? adder_1_out : 8'bz;  // Controlled_Buffer controlled_buffer_8
  assign controlled_buffer_9_out = R_WB ? {DATA7__R, DATA6__R, DATA5__R, DATA4__R, DATA3__R, DATA2__R, DATA1__R, DATA0__R} : 8'bz;  // Controlled_Buffer controlled_buffer_9
  assign DA = and_1_out ? mpu_prg_emulation_1_da : 1'bz;  // Controlled_Buffer controlled_buffer_10
  assign PA = and_1_out ? mpu_prg_emulation_1_pa : 1'bz;  // Controlled_Buffer controlled_buffer_11
  Pull_Resistor pull_resistor_1 (.node(ADDR16));
  assign DA = not_2_out ? mpu_int_emulation_1_pa : 1'bz;  // Controlled_Buffer controlled_buffer_12
  assign PA = not_2_out ? mpu_int_emulation_1_da : 1'bz;  // Controlled_Buffer controlled_buffer_13

  assign ADDR17 = ADDR16;
  assign ADDR18 = ADDR16;
  assign ADDR19 = ADDR16;
  assign ADDR20 = ADDR16;
  assign ADDR21 = ADDR16;
  assign ADDR22 = ADDR16;
  assign ADDR23 = ADDR16;
endmodule

module Interrupt_Decode (
  input  VPB,
  input  INT0,
  input  INT1,
  input  INT2,
  input  INT3,
  input  INT4,
  input  INT5,
  input  INT6,
  input  INT7,
  input  INT8,
  input  INT9,
  input  INT10,
  input  INT11,
  input  INT12,
  input  INT13,
  input  INT14,
  input  INT15,
  output INT_ADDR0,
  output INT_ADDR1,
  output INT_ADDR2,
  output INT_ADDR3,
  output INT
);

  wire and_1_out, and_2_out, not_1_out, not_2_out, pull_resistor_2_node, pull_resistor_4_node, undriven,
       undriven_2;
  wire [3:0] controlled_buffer_1_out, pull_resistor_1_node, pull_resistor_3_node, register_1_q;

  Pull_Resistor pull_resistor_1 (.node(pull_resistor_1_node[3]));
  assign controlled_buffer_1_out = and_1_out ? pull_resistor_1_node : 4'bz;  // Controlled_Buffer controlled_buffer_1
  and and_1 (and_1_out, undriven, not_1_out);
  not not_1 (not_1_out, undriven_2);
  // Probe on pull_resistor_1_node[2:0]
  Priority_Encoder #(.disabled(0)) priority_encoder_1 (
    .in0(INT0), .in1(INT1), .in2(INT2), .in3(INT3), .in4(INT4), .in5(INT5), .in6(INT6), .in7(INT7),
    .out(pull_resistor_1_node[2:0]), .en_in(pull_resistor_2_node));
  Pull_Resistor #(.pull(1)) pull_resistor_2 (.node(pull_resistor_2_node));
  Pull_Resistor #(.pull(1)) pull_resistor_3 (.node(pull_resistor_3_node[3]));
  // Probe on pull_resistor_3_node[2:0]
  Priority_Encoder #(.disabled(0)) priority_encoder_2 (
    .in0(INT8), .in1(INT9), .in2(INT10), .in3(INT11), .in4(INT12), .in5(INT13), .in6(INT14), .in7(INT15),
    .out(pull_resistor_3_node[2:0]), .en_in(pull_resistor_4_node));
  // Probe on controlled_buffer_1_out
  // Probe on controlled_buffer_1_out
  assign controlled_buffer_1_out = undriven_2 ? pull_resistor_3_node : 4'bz;  // Controlled_Buffer controlled_buffer_2
  Pull_Resistor #(.pull(1)) pull_resistor_4 (.node(pull_resistor_4_node));
  // Probe on controlled_buffer_1_out
  and and_2 (and_2_out, not_2_out, INT);
  not not_2 (not_2_out, VPB);
  or or_1 (INT, undriven, undriven_2);
  assign {INT_ADDR3, INT_ADDR2, INT_ADDR1, INT_ADDR0} = INT ? register_1_q : 4'bz;  // Controlled_Buffer controlled_buffer_3
  Register #(.width(4), .trigger("high")) register_1 (
    .D(controlled_buffer_1_out), .Q(register_1_q), .clk(and_2_out));  // open: en, clr
endmodule

module Interrupt_Select (
  input  INT_ADDR0,
  input  INT_ADDR1,
  input  INT_ADDR2,
  input  INT_ADDR3,
  input  INT,
  input  Write,
  input  D0,
  input  D1,
  input  D2,
  input  D3,
  input  D4,
  input  D5,
  input  D6,
  input  D7,
  output NMI,
  output IRQ
);

  wire IRQ0_q, IRQ1_q, IRQ2_q, IRQ3_q, IRQ4_q, IRQ5_q, IRQ6_q, IRQ7_q, multiplexer_1_out, not_1_out,
       not_2_out, not_3_out, or_1_out, or_2_out, or_3_out, pull_resistor_1_node;

  not not_1 (not_1_out, INT);
  not not_2 (not_2_out, Write);
  D_Flip_Flop #(.trigger("high")) IRQ0 (.clk(not_2_out), .D(D0), .Q(IRQ0_q));  // open: Qn, preset, en, reset
  D_Flip_Flop #(.trigger("high")) IRQ1 (.clk(not_2_out), .D(D1), .Q(IRQ1_q));  // open: Qn, preset, en, reset
  D_Flip_Flop #(.trigger("high")) IRQ2 (.clk(not_2_out), .D(D2), .Q(IRQ2_q));  // open: Qn, preset, en, reset
  D_Flip_Flop #(.trigger("high")) IRQ3 (.clk(not_2_out), .D(D3), .Q(IRQ3_q));  // open: Qn, preset, en, reset
  D_Flip_Flop #(.trigger("high")) IRQ4 (.clk(not_2_out), .D(D4), .Q(IRQ4_q));  // open: Qn, preset, en, reset
  D_Flip_Flop #(.trigger("high")) IRQ5 (.clk(not_2_out), .D(D5), .Q(IRQ5_q));  // open: Qn, preset, en, reset
  D_Flip_Flop #(.trigger("high")) IRQ6 (.clk(not_2_out), .D(D6), .Q(IRQ6_q));  // open: Qn, preset, en, reset
  D_Flip_Flop #(.trigger("high")) IRQ7 (.clk(not_2_out), .D(D7), .Q(IRQ7_q));  // open: Qn, preset, en, reset
  // Probe on {INT_ADDR2, INT_ADDR1, INT_ADDR0}
  Pull_Resistor #(.pull(1)) pull_resistor_1 (.node(pull_resistor_1_node));
  or or_1 (or_1_out, INT_ADDR3, multiplexer_1_out);
  Multiplexer #(.select(3)) multiplexer_1 (
    .in0(IRQ0_q), .in1(IRQ1_q), .in2(IRQ2_q), .in3(IRQ3_q), .in4(IRQ4_q), .in5(IRQ5_q), .in6(IRQ6_q),
    .in7(IRQ7_q), .out(multiplexer_1_out), .sel({INT_ADDR2, INT_ADDR1, INT_ADDR0}), .en(pull_resistor_1_node));
  not not_3 (not_3_out, or_1_out);
  or or_2 (or_2_out, not_1_out, or_1_out);
  not not_4 (NMI, or_2_out);
  not not_5 (IRQ, or_3_out);
  or or_3 (or_3_out, not_3_out, not_1_out);
endmodule

module Interrupt_Latch (
  input  PHI2,
  input  INT,
  input  INT_ADDR0,
  input  INT_ADDR1,
  input  INT_ADDR2,
  input  INT_ADDR3,
  input  NMI,
  input  IRQ,
  output LINT_ADDR1,
  output LINT_ADDR2,
  output LINT_ADDR3,
  output LINT_ADDR4,
  output LINT_ADDR5,
  output LINT_ADDR6,
  output LINT_ADDR7,
  output IRQB,
  output NMIB
);

  wire and_1_out, d_ff_1_q, not_1_out, or_1_out, or_2_out, pull_resistor_3_node;
  wire [0:0] register_1_q;
  wire [1:0] counter_1_q;
  wire [7:0] pull_resistor_1_node;

  Pull_Resistor pull_resistor_1 (.node(pull_resistor_1_node[0]));
  Pull_Resistor pull_resistor_2 (.node(pull_resistor_1_node[7]));
  Register #(.trigger("high")) register_1 (
    .D({{3{pull_resistor_1_node[7]}}, INT_ADDR3, INT_ADDR2, INT_ADDR1, INT_ADDR0, pull_resistor_1_node[0]}),
    .Q({LINT_ADDR7, LINT_ADDR6, LINT_ADDR5, LINT_ADDR4, LINT_ADDR3, LINT_ADDR2, LINT_ADDR1, register_1_q[0]}),
    .clk(INT));  // open: en, clr
  D_Flip_Flop #(.trigger("high")) d_ff_1 (
    .clk(INT), .D(pull_resistor_3_node), .Q(d_ff_1_q), .reset(not_1_out));  // open: Qn, preset, en
  Pull_Resistor #(.pull(1)) pull_resistor_3 (.node(pull_resistor_3_node));
  D_Flip_Flop #(.trigger("high")) d_ff_2 (.clk(INT), .D(NMI), .Qn(NMIB), .reset(not_1_out));  // open: Q, preset, en
  and and_1 (and_1_out, PHI2, d_ff_1_q);
  D_Flip_Flop #(.trigger("high")) d_ff_3 (.clk(INT), .D(IRQ), .Qn(IRQB), .reset(not_1_out));  // open: Q, preset, en
  Counter #(.width(2), .max('h3)) counter_1 (.Q(counter_1_q), .clk(or_1_out));  // open: load, D, count, carry, clr
  or or_1 (or_1_out, and_1_out, INT);
  or or_2 (or_2_out, counter_1_q[0], counter_1_q[1]);
  not not_1 (not_1_out, or_2_out);

  // Notes on the sheet:
  //   Use two D Flip-flops for the counter
endmodule

module MPU_INT_Emulation (
  input  PHI2,
  input  IRQB,
  input  NMIB,
  output [7:0] IC,
  output [7:0] DATA,
  output BUSY,
  output R_WB,
  output [15:0] ADDR,
  output DA,
  output PA,
  output VPB
);

  wire and_1_out, comparator_1_eq, comparator_2_eq, counter_1_carry, not_1_out, not_2_out, not_3_out,
       not_4_out, range_test_1_out_4, range_test_2_out_4, xnor_1_out;
  wire [7:0] counter_2_q, Write_Data_out;
  wire [15:0] adder_1_out, controlled_buffer_1_out, controlled_buffer_4_out;

  not not_1 (not_1_out, IRQB);
  not not_2 (not_2_out, NMIB);
  and and_1 (and_1_out, not_1_out, NMIB);
  assign controlled_buffer_1_out = not_2_out ? 16'hffea : 16'bz;  // Controlled_Buffer controlled_buffer_1
  assign controlled_buffer_1_out = and_1_out ? 16'hffee : 16'bz;  // Controlled_Buffer controlled_buffer_2
  xnor xnor_1 (xnor_1_out, not_2_out, and_1_out);
  Counter #(.width(3), .max('h7)) counter_1 (
    .Q(IC[2:0]), .carry(counter_1_carry), .clk(PHI2));  // open: load, D, count, clr
  assign controlled_buffer_1_out = xnor_1_out ? 16'hffcc : 16'bz;  // Controlled_Buffer controlled_buffer_3
  Comparator #(.width(3), .mode("unsigned")) comparator_1 (
    .a(IC[2:0]), .b(3'b101), .eq(comparator_1_eq));  // open: gt, lt
  Range_Test range_test_1 (.MIN(3'b010), .MAX(3'b100), .out_4(range_test_1_out_4), .D(IC[2:0]));
  Counter counter_2 (.Q(counter_2_q), .clk(PHI2), .clr(counter_1_carry));  // open: load, D, count, carry
  Range_Test range_test_2 (.MIN(3'b000), .MAX(3'b001), .out_4(range_test_2_out_4), .D(IC[2:0]));
  Range_Test range_test_3 (.MIN(3'b101), .MAX(3'b110), .out_4(PA), .D(IC[2:0]));
  assign controlled_buffer_4_out = comparator_1_eq ? {16{1'b0}} : 16'bz;  // Controlled_Buffer controlled_buffer_4
  not not_3 (not_3_out, comparator_1_eq);
  assign controlled_buffer_4_out = not_3_out ? 16'h1 : 16'bz;  // Controlled_Buffer controlled_buffer_5
  assign DATA = not_4_out ? Write_Data_out : 8'bz;  // Controlled_Buffer controlled_buffer_6
  Random Write_Data (.clk(not_4_out), .out(Write_Data_out));  // open: next, clr
  not not_4 (not_4_out, R_WB);
  Counter #(.width(1), .max('h1)) counter_3 (.Q(R_WB), .clk(counter_1_carry));  // open: load, D, count, carry, clr
  assign ADDR = DA ? {8'h1, counter_2_q} : 16'bz;  // Controlled_Buffer controlled_buffer_7
  or or_1 (DA, range_test_1_out_4, comparator_2_eq);
  Comparator #(.width(3), .mode("unsigned")) comparator_2 (
    .a(IC[2:0]), .b(3'b111), .eq(comparator_2_eq));  // open: gt, lt
  assign ADDR = range_test_2_out_4 ? 16'hcece : 16'bz;  // Controlled_Buffer controlled_buffer_8
  assign ADDR = PA ? adder_1_out : 16'bz;  // Controlled_Buffer controlled_buffer_9
  // Probe on adder_1_out
  Adder #(.width(16)) adder_1 (
    .a(controlled_buffer_1_out), .b(controlled_buffer_4_out), .out(adder_1_out));  // open: cin, cout
  Pull_Resistor pull_resistor_1 (.node(BUSY));
  not not_5 (BUSY, counter_1_carry);
  not not_6 (VPB, PA);
  // Probe on ADDR

  assign IC[7:3] = {5{1'b0}};

  // Notes on the sheet:
  //   DA
  //   None
  //   PA
endmodule

module MPU_PRG_Emulation (
  input  PHI2,
  output [7:0] IC,
  output [7:0] DATA,
  output BUSY,
  output R_WB,
  output [15:0] ADDR,
  output DA,
  output PA
);

  wire comparator_1_eq, comparator_2_eq, counter_1_carry, not_1_out, not_2_out, or_1_out,
       pull_resistor_1_node, range_test_2_out_4, undriven;
  wire [7:0] Write_Data_out;
  wire [15:0] adder_1_out, Address_out, controlled_buffer_1_out, counter_3_q;

  Counter #(.width(3), .max('h7)) counter_1 (
    .Q(IC[2:0]), .carry(counter_1_carry), .clk(PHI2));  // open: load, D, count, clr
  Random #(.width(16)) Address (.clk(counter_1_carry), .next(pull_resistor_1_node), .out(Address_out));  // open: clr
  Pull_Resistor #(.pull(1)) pull_resistor_1 (.node(pull_resistor_1_node));
  Comparator #(.width(3), .mode("unsigned")) comparator_1 (
    .a(IC[2:0]), .b(3'b111), .eq(comparator_1_eq));  // open: gt, lt
  Range_Test range_test_1 (.MIN(3'b000), .MAX(3'b001), .out_4(PA), .D(IC[2:0]));
  or or_1 (or_1_out, counter_1_carry, comparator_2_eq);
  Comparator #(.width(3), .mode("unsigned")) comparator_2 (
    .a(IC[2:0]), .b(3'b001), .eq(comparator_2_eq));  // open: gt, lt
  Range_Test range_test_2 (.MIN(3'b010), .MAX(3'b011), .out_4(range_test_2_out_4), .D(IC[2:0]));
  Range_Test range_test_3 (.MIN(3'b100), .MAX(3'b111), .out_4(DA), .D(IC[2:0]));
  assign controlled_buffer_1_out = comparator_1_eq ? {16{1'b0}} : 16'bz;  // Controlled_Buffer controlled_buffer_1
  not not_1 (not_1_out, comparator_1_eq);
  assign controlled_buffer_1_out = not_1_out ? 16'h1 : 16'bz;  // Controlled_Buffer controlled_buffer_2
  Random Write_Data (.clk(not_2_out), .next(undriven), .out(Write_Data_out));  // open: clr
  assign DATA = not_2_out ? Write_Data_out : 8'bz;  // Controlled_Buffer controlled_buffer_3
  not not_2 (not_2_out, R_WB);
  Counter #(.width(1), .max('h1)) counter_2 (.Q(R_WB), .clk(counter_1_carry));  // open: load, D, count, carry, clr
  assign ADDR = PA ? counter_3_q : 16'bz;  // Controlled_Buffer controlled_buffer_4
  Counter #(.width(16), .max('hffff)) counter_3 (.Q(counter_3_q), .clk(or_1_out));  // open: load, D, count, carry, clr
  assign ADDR = range_test_2_out_4 ? 16'hcece : 16'bz;  // Controlled_Buffer controlled_buffer_5
  assign ADDR = DA ? adder_1_out : 16'bz;  // Controlled_Buffer controlled_buffer_6
  Adder #(.width(16)) adder_1 (.a(Address_out), .b(controlled_buffer_1_out), .out(adder_1_out));  // open: cin, cout
  not not_3 (BUSY, counter_1_carry);
  // Probe on ADDR

  assign IC[7:3] = {5{1'b0}};

  // Notes on the sheet:
  //   PA
  //   None
  //   DA
endmodule

module Range_Test (
  input  [2:0] MIN,
  input  [2:0] D,
  input  [2:0] MAX,
  output out_4
);

  wire comparator_1_eq, comparator_1_gt, comparator_2_eq, comparator_2_lt, or_1_out, or_2_out;

  Comparator #(.width(3), .mode("unsigned")) comparator_1 (
    .a(D), .b(MIN), .gt(comparator_1_gt), .eq(comparator_1_eq));  // open: lt
  Comparator #(.width(3), .mode("unsigned")) comparator_2 (
    .a(D), .b(MAX), .eq(comparator_2_eq), .lt(comparator_2_lt));  // open: gt
  or or_1 (or_1_out, comparator_1_gt, comparator_1_eq);
  or or_2 (or_2_out, comparator_2_eq, comparator_2_lt);
  and and_1 (out_4, or_1_out, or_2_out);
endmodule
