// Logisim project DeviceDecode.circ as structural Verilog: 1 circuit, main circuit main
module main (
  input  [23:0] in_1,
  input  in_2,
  input  in_3,
  input  in_4
);

  wire AddressValid_B, and_2_out, D32KB_B, D128KB_B, DecodeEnable, NativeMode_B, nor_1_out, OTHER_B, RAM_B,
       RAMCS_B, ROM_B, ROMCS_B;
  wire [7:4] n3_to_8_decoder_lvc138_1_p5;

  // Probe on in_1
  nor nor_1 (nor_1_out, in_1[23], in_1[22], in_1[21]);
  and and_1 (DecodeEnable, in_2, in_3);
  not not_1 (NativeMode_B, in_4);
  not not_2 (AddressValid_B, in_3);
  and and_2 (and_2_out, nor_1_out, in_2);
  or or_1 (OTHER_B, and_2_out, NativeMode_B, AddressValid_B);
  // _3_to_8_Decoder__LVC138 3_to_8_decoder_lvc138_1: pin names not known; wires that end beside it: in_1[23], in_1[22], in_1[21:19], DecodeEnable, {n3_to_8_decoder_lvc138_1_p5, D128KB_B, D32KB_B, ROM_B, RAM_B}
  // _4_bit_Line_Driver__LVC125 4_bit_line_driver_lvc125_1: pin names not known; wires that end beside it: NativeMode_B, NativeMode_B, in_4, in_4, RAM_B, ROM_B, RAM_B, ROM_B, RAMCS_B, ROMCS_B, ROMCS_B, RAMCS_B

  // Other names for the same wires on the sheet: A19 = in_1[19]; A20 = in_1[20]; A21 = in_1[21]; AddressValid = in_3;
  //   A22 = in_1[22]; A23 = in_1[23]; KernalMode = in_2; NativeMode = in_4
endmodule
