// Logisim project DivideBy3.circ as structural Verilog: 1 circuit, main circuit main
module main (
  input  Seleckt
);

  wire and_1_out, and_2_out, and_3_out, and_4_out, and_5_out, buffer_1_out, Clock1, Clock2, clock_1_out,
       d_ff_1_q, d_ff_1_qn, d_ff_2_q, d_ff_2_qn, d_ff_3_qn, d_ff_4_q, d_ff_5_q, d_ff_6_q, d_ff_7_q,
       decoder_1_out0, nand_1_out, not_1_out, not_2_out, not_3_out, not_4_out, or_1_out;
  wire [3:0] counter_1_q;

  Clock clock_1 (.out(clock_1_out));
  buf buffer_1 (buffer_1_out, clock_1_out);
  not not_1 (not_1_out, clock_1_out);
  and and_1 (and_1_out, d_ff_2_qn, d_ff_1_qn);
  Counter #(.max('hf), .width(4)) counter_1 (
    .Q(counter_1_q), .clk(clock_1_out));  // open: load, D, count, carry, up, clr
  D_Flip_Flop d_ff_1 (.clk(buffer_1_out), .D(and_1_out), .Q(d_ff_1_q), .Qn(d_ff_1_qn));  // open: preset, reset
  Decoder #(.select(2)) decoder_1 (.out0(decoder_1_out0), .sel(counter_1_q[2:1]));  // open: out1, out2, out3, en
  D_Flip_Flop d_ff_2 (.clk(buffer_1_out), .D(d_ff_1_q), .Q(d_ff_2_q), .Qn(d_ff_2_qn));  // open: preset, reset
  D_Flip_Flop d_ff_3 (.clk(not_1_out), .D(d_ff_2_q), .Qn(d_ff_3_qn));  // open: Q, preset, reset
  not not_2 (not_2_out, Seleckt);
  and and_2 (and_2_out, not_2_out, not_3_out);
  not not_3 (not_3_out, d_ff_7_q);
  not not_4 (not_4_out, d_ff_6_q);
  and and_3 (and_3_out, not_4_out, Seleckt);
  nand nand_1 (nand_1_out, d_ff_3_qn, d_ff_2_qn);
  not not_5 (Clock1, nand_1_out);
  not not_6 (Clock2, decoder_1_out0);
  D_Flip_Flop d_ff_4 (.clk(Clock1), .D(and_2_out), .Q(d_ff_4_q));  // open: Qn, preset, reset
  D_Flip_Flop d_ff_5 (.clk(Clock2), .D(and_3_out), .Q(d_ff_5_q));  // open: Qn, preset, reset
  D_Flip_Flop d_ff_6 (.clk(Clock1), .D(d_ff_4_q), .Q(d_ff_6_q));  // open: Qn, preset, reset
  D_Flip_Flop d_ff_7 (.clk(Clock2), .D(d_ff_5_q), .Q(d_ff_7_q));  // open: Qn, preset, reset
  and and_4 (and_4_out, Clock1, d_ff_6_q);
  or or_1 (or_1_out, and_4_out, and_5_out);
  and and_5 (and_5_out, Clock2, d_ff_7_q);
  // Digital_Oscilloscope #(.nState(24)) digital_oscilloscope_1: pin names not known; wires that end beside it: buffer_1_out, Clock1, Clock2, or_1_out
endmodule
