// Logisim project Simple_65816.circ as structural Verilog: 1 circuit, main circuit main
module main (
);

  wire and_1_out, clock_1_out, d_ff_1_q, d_ff_2_q, d_ff_3_q, d_ff_4_q, IRQ_B, microprocessor_w65c816_1_p7,
       microprocessor_w65c816_1_p8, microprocessor_w65c816_1_p10, microprocessor_w65c816_1_p11,
       microprocessor_w65c816_1_p12, n8_bit_comparator_f521_1_p4, n8_bit_comparator_f521_2_p3,
       n8_bit_latch_lvc573_1_p3, nand_1_out, NMI_B, not_1_out, not_2_out, not_3_out, not_4_out,
       pull_resistor_1_node, pull_resistor_4_node, pull_resistor_5_node, RDY, RESET, VPB, xor_1_out;
  wire [7:0] D;
  wire [23:0] microprocessor_w65c816_1_p6;

  Pull_Resistor #(.pull(1)) pull_resistor_1 (.node(pull_resistor_1_node));
  Clock clock_1 (.out(clock_1_out));
  not not_1 (not_1_out, clock_1_out);
  // Microprocessor__W65C816 microprocessor_w65c816_1: pin names not known; wires that end beside it: pull_resistor_1_node, IRQ_B, NMI_B, RESET, clock_1_out, microprocessor_w65c816_1_p6[15:0], microprocessor_w65c816_1_p7, microprocessor_w65c816_1_p8, RDY, microprocessor_w65c816_1_p10, microprocessor_w65c816_1_p11, microprocessor_w65c816_1_p12, VPB
  // Probe on microprocessor_w65c816_1_p6[15:0]
  // Probe on microprocessor_w65c816_1_p7
  nand nand_1 (nand_1_out, microprocessor_w65c816_1_p10, microprocessor_w65c816_1_p11);
  Pull_Resistor #(.pull(1)) pull_resistor_2 (.node(microprocessor_w65c816_1_p12));
  D_Flip_Flop d_ff_1 (.clk(not_1_out), .D(microprocessor_w65c816_1_p6[0]), .Q(d_ff_1_q));  // open: Qn, preset, reset
  D_Flip_Flop d_ff_2 (.clk(not_1_out), .D(nand_1_out), .Q(d_ff_2_q));  // open: Qn, preset, reset
  Pull_Resistor pull_resistor_3 ();  // open: node
  not not_2 (not_2_out, nand_1_out);
  Pull_Resistor pull_resistor_4 (.node(pull_resistor_4_node));
  xor xor_1 (xor_1_out, microprocessor_w65c816_1_p6[0], d_ff_1_q);
  not not_3 (not_3_out, d_ff_2_q);
  // _8_bit_Latch__LVC573 8_bit_latch_lvc573_1: pin names not known; wires that end beside it: D, not_2_out, n8_bit_latch_lvc573_1_p3
  and and_1 (and_1_out, xor_1_out, not_3_out);
  // _8_bit_Latch__LVC573 8_bit_latch_lvc573_2: pin names not known; wires that end beside it: pull_resistor_4_node, microprocessor_w65c816_1_p7, not_1_out, microprocessor_w65c816_1_p6[23:16]
  // _8_bit_Bus_Transceiver__LVC4245 8_bit_bus_transceiver_lvc4245_1: pin names not known; wires that end beside it: not_1_out, microprocessor_w65c816_1_p7, microprocessor_w65c816_1_p8, D
  Pull_Resistor pull_resistor_5 (.node(pull_resistor_5_node));
  Pull_Resistor pull_resistor_6 ();  // open: node
  // _8_bit_Comparator__F521 8_bit_comparator_f521_1: pin names not known; wires that end beside it: pull_resistor_5_node, n8_bit_latch_lvc573_1_p3, 8'hab, n8_bit_comparator_f521_1_p4
  // _8_bit_Comparator__F521 8_bit_comparator_f521_2: pin names not known; wires that end beside it: n8_bit_latch_lvc573_1_p3, 8'h5c, n8_bit_comparator_f521_2_p3, n8_bit_comparator_f521_2_p3
  // Probe on microprocessor_w65c816_1_p6[23:16]
  not not_4 (not_4_out, microprocessor_w65c816_1_p8);
  // NOT_Gate not_5 has open pins: in=n8_bit_comparator_f521_1_p4, out=open
  // Probe on microprocessor_w65c816_1_p6[16:0]
  RAM #(.addrWidth(17), .databus("bidir"), .enables("line"), .trigger("high"), .\type ("nonvolatile")) ram_1 (
    .addr(microprocessor_w65c816_1_p6[16:0]), .data(D));  // open: we, oe, clk
  // NOT_Gate not_6 has open pins: in=not_4_out, out=open
  // NOT_Gate not_7 has open pins: in=microprocessor_w65c816_1_p8, out=open
  // NOT_Gate not_8 has open pins: in=not_1_out, out=open
  D_Flip_Flop d_ff_3 (.clk(not_1_out), .D(and_1_out), .Q(d_ff_3_q));  // open: Qn, preset, reset
  D_Flip_Flop d_ff_4 (.clk(not_1_out), .D(d_ff_3_q), .Q(d_ff_4_q));  // open: Qn, preset, reset
  D_Flip_Flop d_ff_5 (.clk(not_1_out), .D(d_ff_4_q));  // open: Q, Qn, preset, reset
  // Probe on D
endmodule
