// Logisim project functional_tests.circ as structural Verilog: 2 circuits, main circuit main
module main (
);

  wire and_1_out, and_2_out, buffer_2_out, buffer_3_out, buffer_4_out, buffer_5_out, buffer_6_out,
       buffer_7_out, buffer_8_out, buffer_9_out, buffer_10_out, buffer_11_out, NMI_out, not_1_out, not_2_out,
       not_3_out, not_4_out, not_5_out, or_1_out, PHI2, pull_resistor_1_node, pull_resistor_2_node,
       Reset_out, start_address_1_active, Success, w65c02s_simple_1_p5;
  wire [7:0] controlled_buffer_1_out, ram_1_dout, w65c02s_simple_1_p6;
  wire [15:0] w65c02s_simple_1_p7;
  wire [23:0] Clock_Count;

  Counter #(.max('hffffff), .width(24)) counter_1 (
    .Q(Clock_Count), .clk(PHI2));  // open: load, D, count, carry, up, clr
  Clock clock_1 (.out(PHI2));
  Button NMI (.out(NMI_out));
  Button Reset (.out(Reset_out));
  Pull_Resistor #(.pull(1)) pull_resistor_1 (.node(pull_resistor_1_node));
  buf buffer_1 (pull_resistor_1_node, buffer_2_out);
  buf buffer_2 (buffer_2_out, buffer_3_out);
  buf buffer_3 (buffer_3_out, buffer_4_out);
  buf buffer_4 (buffer_4_out, buffer_5_out);
  buf buffer_5 (buffer_5_out, buffer_6_out);
  buf buffer_6 (buffer_6_out, buffer_11_out);
  not not_1 (not_1_out, Success);
  and and_1 (and_1_out, not_1_out, PHI2);
  or or_1 (or_1_out, Reset_out, pull_resistor_1_node);
  buf buffer_7 (buffer_7_out, 1'b0);
  Pull_Resistor #(.pull(1)) pull_resistor_2 (.node(pull_resistor_2_node));
  buf buffer_8 (buffer_8_out, buffer_7_out);
  buf buffer_9 (buffer_9_out, buffer_8_out);
  buf buffer_10 (buffer_10_out, buffer_9_out);
  buf buffer_11 (buffer_11_out, buffer_10_out);
  not not_2 (not_2_out, pull_resistor_2_node);
  not not_3 (not_3_out, NMI_out);
  not not_4 (not_4_out, or_1_out);
  // W65C02S__Simple w65c02s_simple_1: pin names not known; wires that end beside it: and_1_out, not_2_out, not_3_out, not_4_out, w65c02s_simple_1_p5, w65c02s_simple_1_p6, w65c02s_simple_1_p7
  not not_5 (not_5_out, w65c02s_simple_1_p5);
  Comparator #(.width(16)) comparator_1 (.a(w65c02s_simple_1_p7), .b(16'h3469), .eq(Success));  // open: gt, lt
  assign controlled_buffer_1_out = not_5_out ? w65c02s_simple_1_p6 : 8'bz;  // Controlled_Buffer controlled_buffer_1
  LED u_Success (.in(Success));
  RAM #(.addrWidth(16), .enables("line")) ram_1 (
    .addr(w65c02s_simple_1_p7), .we(not_5_out), .clk(PHI2), .din(controlled_buffer_1_out), .dout(ram_1_dout));
  // Probe on w65c02s_simple_1_p7
  // Probe on w65c02s_simple_1_p6
  LED Read (.in(w65c02s_simple_1_p5));
  LED Write (.in(w65c02s_simple_1_p5));
  and and_2 (and_2_out, w65c02s_simple_1_p5, start_address_1_active);
  start_address start_address_1 (
    .Data(w65c02s_simple_1_p6), .Active(start_address_1_active), .Clock(PHI2), .Address(16'h400));
  assign w65c02s_simple_1_p6 = and_2_out ? ram_1_dout : 8'bz;  // Controlled_Buffer controlled_buffer_2

  // Notes on the sheet:
  //   (automatic
  //   reset
  //   sequencer)
  //   Address
  //   Data
endmodule

module start_address (
  input  Clock,
  input  [15:0] Address,
  output [7:0] Data,
  output Active
);

  wire comparator_1_eq, comparator_2_eq, or_1_out;
  wire [23:0] counter_1_q;

  Counter #(.max('hffffff), .width(24)) counter_1 (
    .Q(counter_1_q), .clk(Clock));  // open: load, D, count, carry, up, clr
  assign Data = comparator_1_eq ? Address[7:0] : 8'bz;  // Controlled_Buffer controlled_buffer_1
  Comparator #(.width(24)) comparator_1 (.a(counter_1_q), .b(24'h5), .eq(comparator_1_eq));  // open: gt, lt
  assign Data = comparator_2_eq ? Address[15:8] : 8'bz;  // Controlled_Buffer controlled_buffer_2
  Comparator #(.width(24)) comparator_2 (.a(counter_1_q), .b(24'h6), .eq(comparator_2_eq));  // open: gt, lt
  or or_1 (or_1_out, comparator_1_eq, comparator_2_eq);
  not not_1 (Active, or_1_out);
endmodule
