// Logisim project Test.circ as structural Verilog: 1 circuit, main circuit main
module main (
);

  wire clock_1_out, clock_2_out, clock_3_out, clock_4_out, clock_5_out, clock_6_out, clock_7_out,
       clock_8_out, clock_9_out, clock_10_out, clock_11_out, clock_12_out, clock_13_out, clock_14_out,
       clock_15_out, clock_16_out, clock_17_out, clock_18_out, clock_19_out, clock_20_out, clock_21_out,
       clock_22_out, clock_23_out, clock_24_out, comparator_1_eq, comparator_2_eq, comparator_3_eq,
       comparator_4_eq, counter_10_carry, counter_13_carry, decoder_1_out0, decoder_1_out1, decoder_1_out2,
       decoder_1_out3, decoder_1_out4, decoder_1_out5, decoder_1_out6, decoder_1_out7, decoder_2_out0,
       decoder_2_out1, decoder_2_out2, decoder_2_out3, decoder_3_out0, decoder_3_out1, decoder_3_out2,
       decoder_3_out3, ds1813_1_p2, f251_1_p4, f251_1_p5, f283_1_p4, f283_1_p5, f521_1_p4, hc590_1_p6,
       hc590_1_p7, hc4040_1_p3, ls148_1_p3, ls148_1_p4, ls148_1_p5, lvc126_1_p11, lvc126_1_p12, lvc126_1_p13,
       lvc126_1_p14, lvc161_1_p8, lvc161_1_p9, lvc163_1_p7, lvc257_1_p5, lvc373_1_p2, lvc373_1_p4,
       lvc541_1_p1, lvc541_1_p5, lvc543_1_p1, lvc543_1_p6, lvc543_1_p7, lvc543_2_p1, lvc543_2_p5,
       lvc573_1_p2, lvc573_1_p4, lvc16244_1_p11, lvc16244_1_p12, lvc16244_1_p13, lvc16244_1_p14,
       lvc16373_1_p3, lvc16373_1_p7, lvc16373_1_p8, lvc162373_1_p3, lvc162373_1_p7, lvc162373_1_p8,
       not_1_out, not_2_out, not_3_out, not_4_out, not_5_out, not_6_out, not_15_out, not_16_out, not_17_out,
       not_18_out, not_19_out, not_20_out, not_21_out, not_22_out, not_23_out, pull_resistor_1_node,
       pull_resistor_3_node, pull_resistor_5_node, pull_resistor_6_node, pull_resistor_7_node,
       pull_resistor_8_node, pull_resistor_9_node, undriven;
  wire [1:0] counter_11_q, counter_17_q, counter_18_q, counter_22_q;
  wire [2:0] counter_7_q, counter_10_q, counter_21_q;
  wire [3:0] controlled_buffer_7_out, controlled_buffer_8_out, counter_1_q, counter_2_q, counter_3_q,
       counter_4_q, counter_5_q, counter_6_q, counter_8_q, counter_12_q, counter_14_q, counter_15_q,
       counter_16_q, counter_20_q, lsf0204_1_p1, lsf0204_1_p4, lvc126_1_p2, lvc163_1_p6;
  wire [4:0] counter_9_q, counter_13_q, pull_resistor_4_node;
  wire [7:0] controlled_buffer_1_out, controlled_buffer_2_out, controlled_buffer_3_out,
       controlled_buffer_4_out, controlled_buffer_5_out, controlled_buffer_6_out, lvc4245_1_p1, lvc4245_1_p5,
       lvc164245_1_p1, lvc164245_1_p9, not_7_out;
  wire [8:0] counter_19_q;
  wire [15:0] lvc16244_1_p2;

  Random random_1 ();  // open: clk, next, out, clr
  Clock clock_1 (.out(clock_1_out));
  Random random_2 ();  // open: clk, next, out, clr
  Clock clock_2 (.out(clock_2_out));
  Clock clock_3 (.out(clock_3_out));
  Clock clock_4 (.out(clock_4_out));
  Clock clock_5 (.out(clock_5_out));
  Clock clock_6 (.out(clock_6_out));
  Counter #(.max('hf), .width(4)) counter_1 (
    .Q(counter_1_q), .clk(clock_1_out));  // open: load, D, count, carry, up, clr
  Counter #(.max('hf), .width(4)) counter_2 (
    .Q(counter_2_q), .clk(clock_2_out));  // open: load, D, count, carry, up, clr
  Counter #(.max('hf), .width(4)) counter_3 (
    .Q(counter_3_q), .clk(clock_3_out));  // open: load, D, count, carry, up, clr
  Random random_3 (.clr(clock_3_out));  // open: clk, next, out
  Counter #(.max('hf), .width(4)) counter_4 (
    .Q(counter_4_q), .clk(clock_4_out));  // open: load, D, count, carry, up, clr
  Random random_4 (.clr(clock_4_out));  // open: clk, next, out
  Counter #(.max('hf), .width(4)) counter_5 (
    .Q(counter_5_q), .clk(clock_5_out));  // open: load, D, count, carry, up, clr
  // Random random_5: pin names not known; wires that end beside it: clock_5_out
  Counter #(.max('hf), .width(4)) counter_6 (
    .Q(counter_6_q), .clk(clock_6_out));  // open: load, D, count, carry, up, clr
  // Random #(.seed(2)) random_6: pin names not known; wires that end beside it: clock_6_out
  Pull_Resistor #(.pull(1)) pull_resistor_1 (.node(pull_resistor_1_node));
  // Probe on controlled_buffer_1_out
  assign controlled_buffer_1_out = counter_5_q[3] ? lvc4245_1_p1 : 8'bz;  // Controlled_Buffer controlled_buffer_1
  // Probe on controlled_buffer_2_out
  assign controlled_buffer_2_out = counter_6_q[3] ? lvc164245_1_p1 : 8'bz;  // Controlled_Buffer controlled_buffer_2
  // Probe on controlled_buffer_3_out
  assign controlled_buffer_3_out = counter_6_q[2] ? lvc164245_1_p1 : 8'bz;  // Controlled_Buffer controlled_buffer_3
  // Probe on lvc543_2_p5
  not not_1 (not_1_out, counter_5_q[3]);
  not not_2 (not_2_out, counter_6_q[3]);
  not not_3 (not_3_out, counter_6_q[2]);
  Clock clock_7 (.out(clock_7_out));
  // LVC16373 lvc16373_1: pin names not known; wires that end beside it: counter_1_q[0], counter_1_q[1], lvc16373_1_p3, counter_1_q[2], lvc16373_1_p3, counter_1_q[3], lvc16373_1_p7, lvc16373_1_p8
  // LVC573 lvc573_1: pin names not known; wires that end beside it: counter_2_q[0], lvc573_1_p2, counter_2_q[2], lvc573_1_p4
  // LVC543 lvc543_1: pin names not known; wires that end beside it: lvc543_1_p1, counter_3_q[1], counter_3_q[2], counter_3_q[3], lvc543_1_p1, lvc543_1_p6, lvc543_1_p7, lvc543_1_p7
  // LVC543 lvc543_2: pin names not known; wires that end beside it: lvc543_2_p1, pull_resistor_1_node, pull_resistor_1_node, pull_resistor_1_node, lvc543_2_p5, lvc543_2_p1, counter_4_q[1], counter_4_q[2], counter_4_q[3]
  // LVC4245 lvc4245_1: pin names not known; wires that end beside it: lvc4245_1_p1, counter_5_q[0], controlled_buffer_1_out, not_1_out, lvc4245_1_p5
  // LVC164245 lvc164245_1: pin names not known; wires that end beside it: lvc164245_1_p1, counter_6_q[0], counter_6_q[0], counter_6_q[1], controlled_buffer_2_out, not_2_out, controlled_buffer_3_out, not_3_out, lvc164245_1_p9
  // DS1813 ds1813_1: pin names not known; wires that end beside it: clock_7_out, ds1813_1_p2
  // Probe on lvc16373_1_p7
  // Probe on lvc16373_1_p8
  // Probe on lvc573_1_p4
  // Probe on lvc543_1_p6
  Pull_Resistor #(.pull(1)) pull_resistor_2 (.node(lvc543_1_p7));
  // Probe on controlled_buffer_4_out
  assign controlled_buffer_4_out = not_4_out ? lvc4245_1_p5 : 8'bz;  // Controlled_Buffer controlled_buffer_4
  not not_4 (not_4_out, counter_5_q[3]);
  // Probe on controlled_buffer_5_out
  assign controlled_buffer_5_out = not_6_out ? lvc164245_1_p9 : 8'bz;  // Controlled_Buffer controlled_buffer_5
  // Probe on controlled_buffer_6_out
  assign controlled_buffer_6_out = not_5_out ? lvc164245_1_p9 : 8'bz;  // Controlled_Buffer controlled_buffer_6
  not not_5 (not_5_out, counter_6_q[2]);
  // Random #(.seed(1)) random_7: pin names not known; wires that end beside it: controlled_buffer_4_out, clock_5_out
  not not_6 (not_6_out, counter_6_q[3]);
  // Random #(.seed(3)) random_8: pin names not known; wires that end beside it: controlled_buffer_5_out, controlled_buffer_6_out, clock_6_out
  // Probe on ds1813_1_p2
  Counter #(.max('h7), .width(3)) counter_7 (
    .Q(counter_7_q), .clk(clock_8_out));  // open: load, D, count, carry, up, clr
  Clock clock_8 (.out(clock_8_out));
  Counter #(.max('hf), .width(4)) counter_8 (
    .Q(counter_8_q), .clk(clock_9_out));  // open: load, D, count, carry, up, clr
  Clock clock_9 (.out(clock_9_out));
  Counter #(.max('h1f), .width(5)) counter_9 (
    .Q(counter_9_q), .clk(clock_10_out));  // open: load, D, count, carry, up, clr
  Clock clock_10 (.out(clock_10_out));
  Counter #(.max('h7), .width(3)) counter_10 (
    .Q(counter_10_q), .carry(counter_10_carry), .clk(clock_11_out));  // open: load, D, count, up, clr
  Clock clock_11 (.out(clock_11_out));
  Clock clock_12 (.out(clock_12_out));
  Clock clock_13 (.out(clock_13_out));
  Counter #(.max('h3), .width(2)) counter_11 (
    .Q(counter_11_q), .clk(clock_14_out), .clr(undriven));  // open: load, D, count, carry, up
  Clock clock_14 (.out(clock_14_out));
  Pull_Resistor pull_resistor_3 (.node(pull_resistor_3_node));
  not not_7 (not_7_out[0], decoder_1_out0);
  not not_8 (not_7_out[1], decoder_1_out1);
  not not_9 (not_7_out[2], decoder_1_out2);
  not not_10 (not_7_out[3], decoder_1_out3);
  not not_11 (not_7_out[4], decoder_1_out4);
  not not_12 (not_7_out[5], decoder_1_out5);
  not not_13 (not_7_out[6], decoder_1_out6);
  not not_14 (not_7_out[7], decoder_1_out7);
  Decoder #(.select(3)) decoder_1 (
    .out0(decoder_1_out0), .out1(decoder_1_out1), .out2(decoder_1_out2), .out3(decoder_1_out3),
    .out4(decoder_1_out4), .out5(decoder_1_out5), .out6(decoder_1_out6), .out7(decoder_1_out7),
    .sel(counter_8_q[2:0]));  // open: en
  Comparator #(.width(5)) comparator_1 (.a(counter_9_q), .b(5'b11100), .eq(comparator_1_eq));  // open: gt, lt
  Comparator #(.width(5)) comparator_2 (.a(counter_9_q), .b(5'b00100), .eq(comparator_2_eq));  // open: gt, lt
  Pull_Resistor pull_resistor_4 (.node(pull_resistor_4_node));
  Comparator #(.width(4)) comparator_3 (.a(4'b1011), .b(lvc163_1_p6), .eq(comparator_3_eq));  // open: gt, lt
  Counter #(.max('hf), .width(4)) counter_12 (
    .Q(counter_12_q), .clk(counter_13_carry));  // open: load, D, count, carry, up, clr
  Counter #(.max('h1f), .width(5)) counter_13 (
    .Q(counter_13_q), .carry(counter_13_carry), .clk(clock_13_out));  // open: load, D, count, up, clr
  Decoder #(.select(2)) decoder_2 (
    .out0(decoder_2_out0), .out1(decoder_2_out1), .out2(decoder_2_out2), .out3(decoder_2_out3),
    .sel(counter_11_q));  // open: en
  Random #(.width(16)) random_9 (.clk(undriven));  // open: next, out, clr
  Pull_Resistor #(.pull(1)) pull_resistor_5 (.node(pull_resistor_5_node));
  not not_15 (not_15_out, comparator_1_eq);
  not not_16 (not_16_out, comparator_2_eq);
  Pull_Resistor #(.pull(1)) pull_resistor_6 (.node(pull_resistor_6_node));
  not not_17 (not_17_out, comparator_3_eq);
  Pull_Resistor #(.pull(1)) pull_resistor_7 (.node(pull_resistor_7_node));
  // LVC138 lvc138_1: pin names not known; wires that end beside it: pull_resistor_3_node, pull_resistor_3_node, counter_7_q, pull_resistor_5_node
  // LS148 ls148_1: pin names not known; wires that end beside it: not_7_out, counter_8_q[3], ls148_1_p3, ls148_1_p4, ls148_1_p5
  // LVC161 lvc161_1: pin names not known; wires that end beside it: pull_resistor_6_node, not_15_out, not_16_out, 4'b1010, clock_10_out, pull_resistor_6_node, pull_resistor_6_node, lvc161_1_p8, lvc161_1_p9
  // F521 f521_1: pin names not known; wires that end beside it: counter_10_carry, {pull_resistor_4_node, counter_10_q}, 8'h3, f521_1_p4
  // LVC163 lvc163_1: pin names not known; wires that end beside it: not_17_out, pull_resistor_7_node, clock_12_out, pull_resistor_7_node, pull_resistor_7_node, lvc163_1_p6, lvc163_1_p7
  // F283 f283_1: pin names not known; wires that end beside it: counter_12_q, counter_13_q[3:0], counter_13_q[4], f283_1_p4, f283_1_p5
  // LVC16244 lvc16244_1: pin names not known; wires that end beside it: clock_14_out, lvc16244_1_p2, decoder_2_out0, decoder_2_out1, decoder_2_out2, decoder_2_out3, lvc16244_1_p2[3:0], lvc16244_1_p2[7:4], lvc16244_1_p2[11:8], lvc16244_1_p2[15:12], lvc16244_1_p11, lvc16244_1_p12, lvc16244_1_p13, lvc16244_1_p14
  // Probe on nothing
  // Probe on ls148_1_p3
  // Probe on ls148_1_p4
  // Probe on ls148_1_p5
  // Probe on lvc161_1_p8
  // Probe on lvc161_1_p9
  // Probe on f521_1_p4
  // Probe on lvc163_1_p6
  // Probe on lvc163_1_p7
  // Probe on f283_1_p4
  // Probe on f283_1_p5
  // Probe on lvc16244_1_p11
  // Probe on lvc16244_1_p12
  // Probe on lvc16244_1_p13
  // Probe on lvc16244_1_p14
  Random random_10 ();  // open: clk, next, out, clr
  Clock clock_15 (.out(clock_15_out));
  Random random_11 ();  // open: clk, next, out, clr
  Clock clock_16 (.out(clock_16_out));
  Clock clock_17 (.out(clock_17_out));
  Clock clock_18 (.out(clock_18_out));
  Counter #(.max('hf), .width(4)) counter_14 (
    .Q(counter_14_q), .clk(clock_15_out));  // open: load, D, count, carry, up, clr
  Counter #(.max('hf), .width(4)) counter_15 (
    .Q(counter_15_q), .clk(clock_16_out));  // open: load, D, count, carry, up, clr
  Counter #(.max('hf), .width(4)) counter_16 (
    .Q(counter_16_q), .clk(clock_17_out));  // open: load, D, count, carry, up, clr
  // Random #(.width(4)) random_12: pin names not known; wires that end beside it: clock_17_out
  Decoder #(.select(2)) decoder_3 (
    .out0(decoder_3_out0), .out1(decoder_3_out1), .out2(decoder_3_out2), .out3(decoder_3_out3),
    .sel(counter_17_q));  // open: en
  Counter #(.max('h3), .width(2)) counter_17 (
    .Q(counter_17_q), .clk(clock_18_out));  // open: load, D, count, carry, up, clr
  Random #(.width(4)) random_13 (.clk(clock_18_out), .next(clock_18_out));  // open: out, clr
  Clock clock_19 (.out(clock_19_out));
  // Probe on controlled_buffer_7_out
  assign controlled_buffer_7_out = counter_16_q[3] ? lsf0204_1_p1 : 4'bz;  // Controlled_Buffer controlled_buffer_7
  Counter #(.max('h3), .width(2)) counter_18 (
    .Q(counter_18_q), .clk(clock_19_out));  // open: load, D, count, carry, up, clr
  // Random random_14: pin names not known; wires that end beside it: clock_19_out
  not not_18 (not_18_out, decoder_3_out0);
  not not_19 (not_19_out, decoder_3_out1);
  not not_20 (not_20_out, decoder_3_out2);
  not not_21 (not_21_out, decoder_3_out3);
  // LVC162373 lvc162373_1: pin names not known; wires that end beside it: counter_14_q[0], counter_14_q[1], lvc162373_1_p3, counter_14_q[2], lvc162373_1_p3, counter_14_q[3], lvc162373_1_p7, lvc162373_1_p8
  // LVC373 lvc373_1: pin names not known; wires that end beside it: counter_15_q[0], lvc373_1_p2, counter_15_q[2], lvc373_1_p4
  // LSF0204 lsf0204_1: pin names not known; wires that end beside it: lsf0204_1_p1, counter_16_q[2], controlled_buffer_7_out, lsf0204_1_p4
  // LVC126 lvc126_1: pin names not known; wires that end beside it: clock_18_out, lvc126_1_p2, not_18_out, not_19_out, not_20_out, not_21_out, lvc126_1_p2[0], lvc126_1_p2[1], lvc126_1_p2[2], lvc126_1_p2[3], lvc126_1_p11, lvc126_1_p12, lvc126_1_p13, lvc126_1_p14
  // LVC541 lvc541_1: pin names not known; wires that end beside it: lvc541_1_p1, counter_18_q[0], counter_18_q[1], lvc541_1_p1, lvc541_1_p5
  // W65C816 w65c816_1: pin names not known
  // Probe on lvc162373_1_p7
  // Probe on lvc162373_1_p8
  // Probe on lvc373_1_p4
  // Probe on controlled_buffer_8_out
  assign controlled_buffer_8_out = not_22_out ? lsf0204_1_p4 : 4'bz;  // Controlled_Buffer controlled_buffer_8
  not not_22 (not_22_out, counter_16_q[3]);
  // Probe on lvc126_1_p11
  // Probe on lvc126_1_p12
  // Probe on lvc126_1_p13
  // Probe on lvc126_1_p14
  // Probe on lvc541_1_p5
  // Random #(.seed(1), .width(4)) random_15: pin names not known; wires that end beside it: controlled_buffer_8_out, clock_17_out
  Counter #(.max('h1ff), .width(9)) counter_19 (
    .Q(counter_19_q), .clk(clock_20_out));  // open: load, D, count, carry, up, clr
  Clock clock_20 (.out(clock_20_out));
  Clock clock_21 (.out(clock_21_out));
  Clock clock_22 (.out(clock_22_out));
  Counter #(.max('hf), .width(4)) counter_20 (
    .Q(counter_20_q), .clk(clock_23_out));  // open: load, D, count, carry, up, clr
  Clock clock_23 (.out(clock_23_out));
  Clock clock_24 (.out(clock_24_out));
  Comparator #(.width(9)) comparator_4 (.a(counter_19_q), .b(9'h1fc), .eq(comparator_4_eq));  // open: gt, lt
  Counter #(.max('h7), .width(3)) counter_21 (
    .Q(counter_21_q), .clk(clock_22_out));  // open: load, D, count, carry, up, clr
  Counter #(.max('h3), .width(2)) counter_22 (
    .Q(counter_22_q), .clk(clock_24_out));  // open: load, D, count, carry, up, clr
  // W65C02S w65c02s_1: pin names not known
  not not_23 (not_23_out, comparator_4_eq);
  Pull_Resistor #(.pull(1)) pull_resistor_8 (.node(pull_resistor_8_node));
  Pull_Resistor pull_resistor_9 (.node(pull_resistor_9_node));
  // HC590 hc590_1: pin names not known; wires that end beside it: not_23_out, pull_resistor_8_node, counter_19_q[1], clock_20_out, counter_19_q[0], hc590_1_p6, hc590_1_p7
  // HC4040 hc4040_1: pin names not known; wires that end beside it: pull_resistor_9_node, clock_21_out, hc4040_1_p3
  // LVC139 lvc139_1: pin names not known; wires that end beside it: counter_21_q[2], counter_21_q[2], counter_21_q[1:0], counter_21_q[1:0]
  // F251 f251_1: pin names not known; wires that end beside it: counter_20_q[0], counter_20_q[3:1], 8'ha5, f251_1_p4, f251_1_p5
  // LVC257 lvc257_1: pin names not known; wires that end beside it: counter_22_q[0], counter_22_q[1], 4'b1010, 4'b0101, lvc257_1_p5
  // Probe on hc590_1_p6
  // Probe on hc590_1_p7
  // Probe on hc4040_1_p3
  // Probe on nothing
  // Probe on nothing
  // Probe on f251_1_p4
  // Probe on f251_1_p5
  // Probe on lvc257_1_p5
endmodule
